// Logisim project ex.circ as structural Verilog: 1 circuit, main circuit main
module main (
  input  S,
  input  R,
  output notQ,
  output Q
);

  nor nor_1 (notQ, S, Q);
  nor nor_2 (Q, notQ, R);
endmodule
