// Logisim project archi_jeu.circ as structural Verilog: 4 circuits, main circuit main
module main (
);

  wire and_1_out, and_2_out, Clear, ClearIF, Clk, comparator_1_gt, comparator_2_eq, IF, INTA, INTR, or_1_out,
       ReadA, ReadB, ReadINTAdr, ReadMem, ReadPC, ReadSP, SetA, SetB, SetIF, SetMem, SetPC, SetRADM, SetSP,
       ual_1_p10;
  wire [1:0] mcounttomux_1_mux;
  wire [2:0] CodeMCount;
  wire [3:0] UAL;
  wire [6:0] keyboard_1_data, register_1_q;
  wire [7:0] adder_1_out, Adr, controlled_buffer_2_out, controlled_buffer_2_out_2, MicroPC_q,
       multiplexer_1_out;
  wire [15:0] A_q, AdrBus, B_q, cartegraphique_1_r0, cartegraphique_1_r1, cartegraphique_1_r2,
       cartegraphique_1_r3, cartegraphique_1_r4, cartegraphique_1_r5, cartegraphique_1_r6,
       cartegraphique_1_r7, cartegraphique_1_r8, cartegraphique_1_r9, cartegraphique_1_r10,
       cartegraphique_1_r11, cartegraphique_1_r12, cartegraphique_1_r13, cartegraphique_1_r14,
       cartegraphique_1_r15, controlled_buffer_1_out, controlled_buffer_4_out, controlled_buffer_7_out,
       controlled_buffer_9_out, controlled_buffer_11_out, controlled_buffer_14_out, DBus, Program_counter_q,
       pull_resistor_2_node, ram_1_data, Stack_Pointer_q, ual_1_p8;
  wire [31:30] rom_1_data;

  assign controlled_buffer_1_out = SetMem ? DBus : 16'bz;  // Controlled_Buffer controlled_buffer_1
  assign {controlled_buffer_2_out_2, controlled_buffer_2_out} = ReadMem ? DBus : 16'bz;  // Controlled_Buffer controlled_buffer_2
  assign DBus = SetMem ? ual_1_p8 : 16'bz;  // Controlled_Buffer controlled_buffer_3
  Comparator #(.width(16), .mode("unsigned")) comparator_1 (
    .a(16'h1000), .b(AdrBus), .gt(comparator_1_gt));  // open: eq, lt
  assign controlled_buffer_4_out = SetRADM ? ual_1_p8 : 16'bz;  // Controlled_Buffer controlled_buffer_4
  RAM #(.addrWidth(16), .dataWidth(16), .bus("separate")) ram_1 (
    .addr(AdrBus), .din(controlled_buffer_1_out), .data(ram_1_data), .str(SetMem), .sel(comparator_1_gt),
    .clk(Clk), .ld(ReadMem));  // open: clr
  assign DBus = ReadMem ? ram_1_data : 16'bz;  // Controlled_Buffer controlled_buffer_5
  Pull_Resistor pull_resistor_1 (.node({controlled_buffer_2_out_2, controlled_buffer_2_out}));
  Pull_Resistor pull_resistor_2 (.node(pull_resistor_2_node));
  Register #(.width(16)) Radm (.D(controlled_buffer_4_out), .en(SetRADM), .Q(AdrBus), .clk(Clk), .clr(Clear));
  assign pull_resistor_2_node = ReadINTAdr ? 16'h2 : 16'bz;  // Controlled_Buffer controlled_buffer_6
  Keyboard #(.buflen(1)) keyboard_1 (.clk(Clk), .re(INTA), .clr(Clear), .avail(INTR), .data(keyboard_1_data));
  Button button_1 (.out(Clear));
  Clock clock_1 (.out(Clk));
  Register #(.width(16)) A (.D(controlled_buffer_7_out), .en(SetA), .Q(A_q), .clk(Clk), .clr(Clear));
  assign controlled_buffer_7_out = SetA ? ual_1_p8 : 16'bz;  // Controlled_Buffer controlled_buffer_7
  assign pull_resistor_2_node = ReadA ? A_q : 16'bz;  // Controlled_Buffer controlled_buffer_8
  assign controlled_buffer_9_out = SetB ? ual_1_p8 : 16'bz;  // Controlled_Buffer controlled_buffer_9
  Comparator #(.width(16), .mode("unsigned")) comparator_2 (
    .a(16'h1003), .b(AdrBus), .eq(comparator_2_eq));  // open: gt, lt
  assign {controlled_buffer_2_out_2, controlled_buffer_2_out} = ReadB ? B_q : 16'bz;  // Controlled_Buffer controlled_buffer_10
  Register #(.width(16)) B (.D(controlled_buffer_9_out), .en(SetB), .Q(B_q), .clk(Clk), .clr(Clear));
  Register #(.width(7)) register_1 (.D(keyboard_1_data), .en(INTA), .Q(register_1_q), .clk(Clk), .clr(Clear));
  and and_1 (and_1_out, ReadMem, comparator_2_eq);
  assign controlled_buffer_11_out = SetPC ? ual_1_p8 : 16'bz;  // Controlled_Buffer controlled_buffer_11
  assign DBus = and_1_out ? {{9{1'b0}}, register_1_q} : 16'bz;  // Controlled_Buffer controlled_buffer_12
  assign pull_resistor_2_node = ReadPC ? Program_counter_q : 16'bz;  // Controlled_Buffer controlled_buffer_13
  Register #(.width(16)) Program_counter (
    .D(controlled_buffer_11_out), .en(SetPC), .Q(Program_counter_q), .clk(Clk), .clr(Clear));
  assign controlled_buffer_14_out = SetSP ? ual_1_p8 : 16'bz;  // Controlled_Buffer controlled_buffer_14
  Adder adder_1 (.a(MicroPC_q), .b(8'h1), .out(adder_1_out), .cin(1'b0));  // open: cout
  Register #(.width(16)) Stack_Pointer (
    .D(controlled_buffer_14_out), .en(SetSP), .Q(Stack_Pointer_q), .clk(Clk), .clr(Clear));
  assign pull_resistor_2_node = ReadSP ? Stack_Pointer_q : 16'bz;  // Controlled_Buffer controlled_buffer_15
  Multiplexer #(.select(2), .width(8)) multiplexer_1 (
    .in0(adder_1_out), .in1(Adr), .in2(controlled_buffer_2_out_2), .out(multiplexer_1_out),
    .sel(mcounttomux_1_mux), .en(1'b1));  // open: in3
  MCountToMux mcounttomux_1 (.INT(and_2_out), .MCount(CodeMCount), .Z(ual_1_p10), .Mux(mcounttomux_1_mux));
  and and_2 (and_2_out, IF, INTR);
  D_Flip_Flop Interrupt_Flag (.clk(Clk), .D(SetIF), .Q(IF), .en(or_1_out), .reset(Clear));  // open: Qn, preset
  or or_1 (or_1_out, ClearIF, ClearIF, SetIF, SetIF);
  CarteGraphique cartegraphique_1 (
    .ABus(AdrBus), .DBus(DBus), .SetMem(SetMem), .Clear(Clear), .Clk(Clk), .R15(cartegraphique_1_r15),
    .R14(cartegraphique_1_r14), .R13(cartegraphique_1_r13), .R12(cartegraphique_1_r12),
    .R11(cartegraphique_1_r11), .R10(cartegraphique_1_r10), .R9(cartegraphique_1_r9),
    .R8(cartegraphique_1_r8), .R7(cartegraphique_1_r7), .R6(cartegraphique_1_r6), .R5(cartegraphique_1_r5),
    .R4(cartegraphique_1_r4), .R3(cartegraphique_1_r3), .R2(cartegraphique_1_r2), .R1(cartegraphique_1_r1),
    .R0(cartegraphique_1_r0));
  DotMatrix #(.inputtype("row"), .matrixcols(16), .matrixrows(16)) dotmatrix_1 (
    .row0(cartegraphique_1_r15), .row1(cartegraphique_1_r14), .row2(cartegraphique_1_r13),
    .row3(cartegraphique_1_r12), .row4(cartegraphique_1_r11), .row5(cartegraphique_1_r10),
    .row6(cartegraphique_1_r9), .row7(cartegraphique_1_r8), .row8(cartegraphique_1_r7),
    .row9(cartegraphique_1_r6), .row10(cartegraphique_1_r5), .row11(cartegraphique_1_r4),
    .row12(cartegraphique_1_r3), .row13(cartegraphique_1_r2), .row14(cartegraphique_1_r1),
    .row15(cartegraphique_1_r0));
  Register MicroPC (.D(multiplexer_1_out), .en(1'b1), .Q(MicroPC_q), .clk(Clk), .clr(Clear));
  // UAL ual_1: pin names not known; wires that end beside it: SetIF, IF, INTR, UAL[1], pull_resistor_2_node, UAL[2], UAL[3], ual_1_p8, {controlled_buffer_2_out_2, controlled_buffer_2_out}, ual_1_p10, ual_1_p10
  ROM #(.dataWidth(32)) rom_1 (
    .addr(MicroPC_q),
    .data({rom_1_data, ReadINTAdr, ClearIF, SetIF, INTA, CodeMCount, UAL, SetSP, ReadSP, SetB, ReadB, SetA, ReadA, SetPC, ReadPC, SetRADM, SetMem, ReadMem, Adr}),
    .sel(1'b1));

  // Notes on the sheet:
  //   Bus Adresse
  //   Bus Données
  //   Bus B
  //   Bus A
  //   InstCode
  //   Bus S
  //   S = 0 ?
  //   contents of rom_1 (hex, n*v repeats v):
  //   2000008 8000e0 6*0 c00 1401900 0 0 80000c 0 0 0 c00 84100 c01800 0 c00 80500 84100 c01800 88400
  //   802200 0 0 c00 80500 2200 c01800 c00 90100 c01800 0 c00 80500 90100 c01800 2400 888200 0 0 c00 80500
  //   8a200 c01800 b0e000 0 0 0 b1a000 0 0 0 b8e000 0 0 0 b9a000 0 0 0 d0e000 0 0 0 d1a000 0 0 0 d86000
  //   7*0 90e000 0 0 0 91a000 0 0 0 98e000 0 0 0 99a000 0 0 0 a06000 0 0 0 a98000 11*0 c00 881100 0 0
  //   1802076 c01800 c00 881100 188807a c01800 c00 881100 4*0 c00 c0100 c01800 0 c00 80500 c0100 c01800
  //   4*0 c00 80500 20200 c01800 c60000 0 0 0 ce0000 11*0 20400 400a00 4e0000 c00 881100 0 0 0 460400
  //   881100 6*0 20400 2200 ce0000 0 460400 884100 0 0 c00 320500 2200 c01800 c00 320500 84100 c01800
  //   20400 88200 ce0000 0 460400 890100 0 0 c00 320500 88200 c01800 c00 320500 90100 c01800 10800000 0 0
  //   0 8800000 11*0 14020400 2200 4e0400 88200 4e0400 a00 4e0000 20801008 460400 81100 460400 90100
  //   460400 8884100
endmodule

module MCountToMux (
  input  INT,
  input  [2:0] MCount,
  input  Z,
  output [1:0] Mux
);

  wire and_2_out, and_3_out, and_4_out, not_1_out, not_2_out, not_3_out, not_4_out;

  not not_1 (not_1_out, INT);
  not not_2 (not_2_out, MCount[1]);
  not not_3 (not_3_out, MCount[0]);
  not not_4 (not_4_out, Z);
  and and_1 (Mux[1], MCount[1], not_3_out);
  and and_2 (and_2_out, not_2_out, MCount[0]);
  and and_3 (and_3_out, MCount[1], MCount[0], Z);
  and and_4 (and_4_out, not_1_out, MCount[2]);
  or or_1 (Mux[0], and_2_out, and_3_out, and_4_out);
endmodule

module Coupleur (
  input  SetMem,
  input  [15:0] DataBus,
  input  [15:0] Adr,
  input  [15:0] AdrBus,
  output [15:0] Data,
  output Enable
);

  wire comparator_1_eq;

  Comparator #(.width(16), .mode("unsigned")) comparator_1 (.a(Adr), .b(AdrBus), .eq(comparator_1_eq));  // open: gt, lt
  and and_1 (Enable, SetMem, comparator_1_eq);
  assign Data = Enable ? DataBus : 16'bz;  // Controlled_Buffer controlled_buffer_1
endmodule

module CarteGraphique (
  input  [15:0] ABus,
  input  [15:0] DBus,
  input  SetMem,
  input  Clear,
  input  Clk,
  output [15:0] R15,
  output [15:0] R14,
  output [15:0] R13,
  output [15:0] R12,
  output [15:0] R11,
  output [15:0] R10,
  output [15:0] R9,
  output [15:0] R8,
  output [15:0] R7,
  output [15:0] R6,
  output [15:0] R5,
  output [15:0] R4,
  output [15:0] R3,
  output [15:0] R2,
  output [15:0] R1,
  output [15:0] R0
);

  wire and_1_out, and_2_out, BSel, coupleur_1_enable, coupleur_2_enable, coupleur_3_enable,
       coupleur_4_enable, coupleur_5_enable, coupleur_6_enable, coupleur_7_enable, coupleur_8_enable,
       coupleur_9_enable, coupleur_10_enable, coupleur_11_enable, coupleur_12_enable, coupleur_13_enable,
       coupleur_14_enable, coupleur_15_enable, coupleur_16_enable, coupleur_17_enable, coupleur_18_enable,
       coupleur_19_enable, coupleur_20_enable, coupleur_21_enable, coupleur_22_enable, coupleur_23_enable,
       coupleur_24_enable, coupleur_25_enable, coupleur_26_enable, coupleur_27_enable, coupleur_28_enable,
       coupleur_29_enable, coupleur_30_enable, coupleur_31_enable, coupleur_32_enable, coupleur_33_enable,
       not_1_out;
  wire [15:0] coupleur_1_data, coupleur_2_data, coupleur_3_data, coupleur_4_data, coupleur_5_data,
       coupleur_6_data, coupleur_7_data, coupleur_8_data, coupleur_9_data, coupleur_10_data,
       coupleur_11_data, coupleur_12_data, coupleur_13_data, coupleur_14_data, coupleur_15_data,
       coupleur_16_data, coupleur_17_data, coupleur_18_data, coupleur_19_data, coupleur_20_data,
       coupleur_21_data, coupleur_22_data, coupleur_23_data, coupleur_24_data, coupleur_25_data,
       coupleur_26_data, coupleur_27_data, coupleur_28_data, coupleur_29_data, coupleur_30_data,
       coupleur_31_data, coupleur_32_data, coupleur_33_data, L0, L1, L2, L3, L4, L5, L6, L7, L8, L9, L10,
       L11, L12, L13, L14, L15, M0, M1, M2, M3, M4, M5, M6, M7, M8, M9, M10, M11, M12, M13, M14, M15;
  wire [15:1] register_17_q;

  Coupleur coupleur_1 (
    .SetMem(SetMem), .DataBus(DBus), .Adr(16'h200c), .AdrBus(ABus), .Data(coupleur_1_data),
    .Enable(coupleur_1_enable));
  Register #(.width(16)) register_1 (
    .D(coupleur_1_data), .en(coupleur_1_enable), .Q(L12), .clk(and_1_out), .clr(Clear));
  Register #(.width(16)) register_2 (.D(coupleur_2_data), .en(coupleur_2_enable), .Q(L8), .clk(and_1_out), .clr(Clear));
  Coupleur coupleur_2 (
    .SetMem(SetMem), .DataBus(DBus), .Adr(16'h2008), .AdrBus(ABus), .Data(coupleur_2_data),
    .Enable(coupleur_2_enable));
  Register #(.width(16)) register_3 (.D(coupleur_3_data), .en(coupleur_3_enable), .Q(L4), .clk(and_1_out), .clr(Clear));
  Coupleur coupleur_3 (
    .SetMem(SetMem), .DataBus(DBus), .Adr(16'h2004), .AdrBus(ABus), .Data(coupleur_3_data),
    .Enable(coupleur_3_enable));
  Coupleur coupleur_4 (
    .SetMem(SetMem), .DataBus(DBus), .Adr(16'h2000), .AdrBus(ABus), .Data(coupleur_4_data),
    .Enable(coupleur_4_enable));
  Coupleur coupleur_5 (
    .SetMem(SetMem), .DataBus(DBus), .Adr(16'h200d), .AdrBus(ABus), .Data(coupleur_5_data),
    .Enable(coupleur_5_enable));
  Register #(.width(16)) register_4 (.D(coupleur_4_data), .en(coupleur_4_enable), .Q(L0), .clk(and_1_out), .clr(Clear));
  Register #(.width(16)) register_5 (
    .D(coupleur_5_data), .en(coupleur_5_enable), .Q(L13), .clk(and_1_out), .clr(Clear));
  Register #(.width(16)) register_6 (.D(coupleur_6_data), .en(coupleur_6_enable), .Q(L9), .clk(and_1_out), .clr(Clear));
  Coupleur coupleur_6 (
    .SetMem(SetMem), .DataBus(DBus), .Adr(16'h2009), .AdrBus(ABus), .Data(coupleur_6_data),
    .Enable(coupleur_6_enable));
  Coupleur coupleur_7 (
    .SetMem(SetMem), .DataBus(DBus), .Adr(16'h2005), .AdrBus(ABus), .Data(coupleur_7_data),
    .Enable(coupleur_7_enable));
  Register #(.width(16)) register_7 (.D(coupleur_7_data), .en(coupleur_7_enable), .Q(L5), .clk(and_1_out), .clr(Clear));
  Coupleur coupleur_8 (
    .SetMem(SetMem), .DataBus(DBus), .Adr(16'h2001), .AdrBus(ABus), .Data(coupleur_8_data),
    .Enable(coupleur_8_enable));
  Register #(.width(16)) register_8 (.D(coupleur_8_data), .en(coupleur_8_enable), .Q(L1), .clk(and_1_out), .clr(Clear));
  Coupleur coupleur_9 (
    .SetMem(SetMem), .DataBus(DBus), .Adr(16'h200e), .AdrBus(ABus), .Data(coupleur_9_data),
    .Enable(coupleur_9_enable));
  Register #(.width(16)) register_9 (
    .D(coupleur_9_data), .en(coupleur_9_enable), .Q(L14), .clk(and_1_out), .clr(Clear));
  Coupleur coupleur_10 (
    .SetMem(SetMem), .DataBus(DBus), .Adr(16'h200a), .AdrBus(ABus), .Data(coupleur_10_data),
    .Enable(coupleur_10_enable));
  Register #(.width(16)) register_10 (
    .D(coupleur_10_data), .en(coupleur_10_enable), .Q(L10), .clk(and_1_out), .clr(Clear));
  Register #(.width(16)) register_11 (
    .D(coupleur_11_data), .en(coupleur_11_enable), .Q(L6), .clk(and_1_out), .clr(Clear));
  Coupleur coupleur_11 (
    .SetMem(SetMem), .DataBus(DBus), .Adr(16'h2006), .AdrBus(ABus), .Data(coupleur_11_data),
    .Enable(coupleur_11_enable));
  Register #(.width(16)) register_12 (
    .D(coupleur_12_data), .en(coupleur_12_enable), .Q(L2), .clk(and_1_out), .clr(Clear));
  Coupleur coupleur_12 (
    .SetMem(SetMem), .DataBus(DBus), .Adr(16'h2002), .AdrBus(ABus), .Data(coupleur_12_data),
    .Enable(coupleur_12_enable));
  Coupleur coupleur_13 (
    .SetMem(SetMem), .DataBus(DBus), .Adr(16'h200f), .AdrBus(ABus), .Data(coupleur_13_data),
    .Enable(coupleur_13_enable));
  Multiplexer #(.width(16), .enable("false")) multiplexer_1 (.in0(L15), .in1(M15), .out(R15), .sel(BSel));
  Multiplexer #(.width(16), .enable("false")) multiplexer_2 (.in0(L14), .in1(M14), .out(R14), .sel(BSel));
  Multiplexer #(.width(16), .enable("false")) multiplexer_3 (.in0(L13), .in1(M13), .out(R13), .sel(BSel));
  Multiplexer #(.width(16), .enable("false")) multiplexer_4 (.in0(L12), .in1(M12), .out(R12), .sel(BSel));
  Register #(.width(16)) register_13 (
    .D(coupleur_13_data), .en(coupleur_13_enable), .Q(L15), .clk(and_1_out), .clr(Clear));
  Coupleur coupleur_14 (
    .SetMem(SetMem), .DataBus(DBus), .Adr(16'h200b), .AdrBus(ABus), .Data(coupleur_14_data),
    .Enable(coupleur_14_enable));
  Register #(.width(16)) register_14 (
    .D(coupleur_14_data), .en(coupleur_14_enable), .Q(L11), .clk(and_1_out), .clr(Clear));
  Register #(.width(16)) register_15 (
    .D(coupleur_15_data), .en(coupleur_15_enable), .Q(L7), .clk(and_1_out), .clr(Clear));
  Coupleur coupleur_15 (
    .SetMem(SetMem), .DataBus(DBus), .Adr(16'h2007), .AdrBus(ABus), .Data(coupleur_15_data),
    .Enable(coupleur_15_enable));
  Coupleur coupleur_16 (
    .SetMem(SetMem), .DataBus(DBus), .Adr(16'h2003), .AdrBus(ABus), .Data(coupleur_16_data),
    .Enable(coupleur_16_enable));
  Register #(.width(16)) register_16 (
    .D(coupleur_16_data), .en(coupleur_16_enable), .Q(L3), .clk(and_1_out), .clr(Clear));
  Multiplexer #(.width(16), .enable("false")) multiplexer_5 (.in0(L11), .in1(M11), .out(R11), .sel(BSel));
  Multiplexer #(.width(16), .enable("false")) multiplexer_6 (.in0(L10), .in1(M10), .out(R10), .sel(BSel));
  Multiplexer #(.width(16), .enable("false")) multiplexer_7 (.in0(L9), .in1(M9), .out(R9), .sel(BSel));
  Multiplexer #(.width(16), .enable("false")) multiplexer_8 (.in0(L8), .in1(M8), .out(R8), .sel(BSel));
  Register #(.width(16)) register_17 (
    .D(coupleur_17_data), .en(coupleur_17_enable), .Q({register_17_q, BSel}), .clk(Clk), .clr(Clear));
  Coupleur coupleur_17 (
    .SetMem(SetMem), .DataBus(DBus), .Adr(16'h2010), .AdrBus(ABus), .Data(coupleur_17_data),
    .Enable(coupleur_17_enable));
  and and_1 (and_1_out, Clk, BSel);
  Multiplexer #(.width(16), .enable("false")) multiplexer_9 (.in0(L7), .in1(M7), .out(R7), .sel(BSel));
  Multiplexer #(.width(16), .enable("false")) multiplexer_10 (.in0(L6), .in1(M6), .out(R6), .sel(BSel));
  Multiplexer #(.width(16), .enable("false")) multiplexer_11 (.in0(L5), .in1(M5), .out(R5), .sel(BSel));
  Multiplexer #(.width(16), .enable("false")) multiplexer_12 (.in0(L4), .in1(M4), .out(R4), .sel(BSel));
  not not_1 (not_1_out, BSel);
  and and_2 (and_2_out, Clk, not_1_out);
  Multiplexer #(.width(16), .enable("false")) multiplexer_13 (.in0(L3), .in1(M3), .out(R3), .sel(BSel));
  Multiplexer #(.width(16), .enable("false")) multiplexer_14 (.in0(L2), .in1(M2), .out(R2), .sel(BSel));
  Multiplexer #(.width(16), .enable("false")) multiplexer_15 (.in0(L1), .in1(M1), .out(R1), .sel(BSel));
  Multiplexer #(.width(16), .enable("false")) multiplexer_16 (.in0(L0), .in1(M0), .out(R0), .sel(BSel));
  Coupleur coupleur_18 (
    .SetMem(SetMem), .DataBus(DBus), .Adr(16'h200c), .AdrBus(ABus), .Data(coupleur_18_data),
    .Enable(coupleur_18_enable));
  Register #(.width(16)) register_18 (
    .D(coupleur_18_data), .en(coupleur_18_enable), .Q(M12), .clk(and_2_out), .clr(Clear));
  Coupleur coupleur_19 (
    .SetMem(SetMem), .DataBus(DBus), .Adr(16'h2008), .AdrBus(ABus), .Data(coupleur_19_data),
    .Enable(coupleur_19_enable));
  Register #(.width(16)) register_19 (
    .D(coupleur_19_data), .en(coupleur_19_enable), .Q(M8), .clk(and_2_out), .clr(Clear));
  Register #(.width(16)) register_20 (
    .D(coupleur_20_data), .en(coupleur_20_enable), .Q(M4), .clk(and_2_out), .clr(Clear));
  Coupleur coupleur_20 (
    .SetMem(SetMem), .DataBus(DBus), .Adr(16'h2004), .AdrBus(ABus), .Data(coupleur_20_data),
    .Enable(coupleur_20_enable));
  Register #(.width(16)) register_21 (
    .D(coupleur_21_data), .en(coupleur_21_enable), .Q(M0), .clk(and_2_out), .clr(Clear));
  Coupleur coupleur_21 (
    .SetMem(SetMem), .DataBus(DBus), .Adr(16'h2000), .AdrBus(ABus), .Data(coupleur_21_data),
    .Enable(coupleur_21_enable));
  Coupleur coupleur_22 (
    .SetMem(SetMem), .DataBus(DBus), .Adr(16'h200d), .AdrBus(ABus), .Data(coupleur_22_data),
    .Enable(coupleur_22_enable));
  Coupleur coupleur_23 (
    .SetMem(SetMem), .DataBus(DBus), .Adr(16'h2009), .AdrBus(ABus), .Data(coupleur_23_data),
    .Enable(coupleur_23_enable));
  Coupleur coupleur_24 (
    .SetMem(SetMem), .DataBus(DBus), .Adr(16'h2005), .AdrBus(ABus), .Data(coupleur_24_data),
    .Enable(coupleur_24_enable));
  Coupleur coupleur_25 (
    .SetMem(SetMem), .DataBus(DBus), .Adr(16'h2001), .AdrBus(ABus), .Data(coupleur_25_data),
    .Enable(coupleur_25_enable));
  Register #(.width(16)) register_22 (
    .D(coupleur_22_data), .en(coupleur_22_enable), .Q(M13), .clk(and_2_out), .clr(Clear));
  Register #(.width(16)) register_23 (
    .D(coupleur_23_data), .en(coupleur_23_enable), .Q(M9), .clk(and_2_out), .clr(Clear));
  Register #(.width(16)) register_24 (
    .D(coupleur_24_data), .en(coupleur_24_enable), .Q(M5), .clk(and_2_out), .clr(Clear));
  Register #(.width(16)) register_25 (
    .D(coupleur_25_data), .en(coupleur_25_enable), .Q(M1), .clk(and_2_out), .clr(Clear));
  Coupleur coupleur_26 (
    .SetMem(SetMem), .DataBus(DBus), .Adr(16'h200e), .AdrBus(ABus), .Data(coupleur_26_data),
    .Enable(coupleur_26_enable));
  Coupleur coupleur_27 (
    .SetMem(SetMem), .DataBus(DBus), .Adr(16'h200a), .AdrBus(ABus), .Data(coupleur_27_data),
    .Enable(coupleur_27_enable));
  Coupleur coupleur_28 (
    .SetMem(SetMem), .DataBus(DBus), .Adr(16'h2006), .AdrBus(ABus), .Data(coupleur_28_data),
    .Enable(coupleur_28_enable));
  Coupleur coupleur_29 (
    .SetMem(SetMem), .DataBus(DBus), .Adr(16'h2002), .AdrBus(ABus), .Data(coupleur_29_data),
    .Enable(coupleur_29_enable));
  Register #(.width(16)) register_26 (
    .D(coupleur_26_data), .en(coupleur_26_enable), .Q(M14), .clk(and_2_out), .clr(Clear));
  Register #(.width(16)) register_27 (
    .D(coupleur_27_data), .en(coupleur_27_enable), .Q(M10), .clk(and_2_out), .clr(Clear));
  Register #(.width(16)) register_28 (
    .D(coupleur_28_data), .en(coupleur_28_enable), .Q(M6), .clk(and_2_out), .clr(Clear));
  Register #(.width(16)) register_29 (
    .D(coupleur_29_data), .en(coupleur_29_enable), .Q(M2), .clk(and_2_out), .clr(Clear));
  Coupleur coupleur_30 (
    .SetMem(SetMem), .DataBus(DBus), .Adr(16'h200f), .AdrBus(ABus), .Data(coupleur_30_data),
    .Enable(coupleur_30_enable));
  Coupleur coupleur_31 (
    .SetMem(SetMem), .DataBus(DBus), .Adr(16'h200b), .AdrBus(ABus), .Data(coupleur_31_data),
    .Enable(coupleur_31_enable));
  Coupleur coupleur_32 (
    .SetMem(SetMem), .DataBus(DBus), .Adr(16'h2007), .AdrBus(ABus), .Data(coupleur_32_data),
    .Enable(coupleur_32_enable));
  Coupleur coupleur_33 (
    .SetMem(SetMem), .DataBus(DBus), .Adr(16'h2003), .AdrBus(ABus), .Data(coupleur_33_data),
    .Enable(coupleur_33_enable));
  Register #(.width(16)) register_30 (
    .D(coupleur_30_data), .en(coupleur_30_enable), .Q(M15), .clk(and_2_out), .clr(Clear));
  Register #(.width(16)) register_31 (
    .D(coupleur_31_data), .en(coupleur_31_enable), .Q(M11), .clk(and_2_out), .clr(Clear));
  Register #(.width(16)) register_32 (
    .D(coupleur_32_data), .en(coupleur_32_enable), .Q(M7), .clk(and_2_out), .clr(Clear));
  Register #(.width(16)) register_33 (
    .D(coupleur_33_data), .en(coupleur_33_enable), .Q(M3), .clk(and_2_out), .clr(Clear));

  // Other names for the same wires on the sheet: AdrBus[15:0] = ABus

  // Notes on the sheet:
  //   Double buffer switch
endmodule
