// Logisim project archi_seq_man_regual.circ as structural Verilog: 1 circuit, main circuit main
module main (
  input  [3:0] UAL,
  input  SetB,
  input  ReadB,
  input  SetA,
  input  ReadA,
  input  SetMem,
  input  ReadMem,
  input  [15:0] Data,
  output S___0
);

  wire Clear, Clk;
  wire [3:0] binarytobcd_1_p2, binarytobcd_1_p3, binarytobcd_1_p4, binarytobcd_1_p5, binarytobcd_1_p6;
  wire [15:0] A_q, B_q, controlled_buffer_1_out, controlled_buffer_2_out, controlled_buffer_3_out,
       controlled_buffer_5_out, pull_resistor_1_node, RO0_q, ual_1_p5;

  Pull_Resistor pull_resistor_1 (.node(pull_resistor_1_node));
  assign controlled_buffer_1_out = ReadMem ? Data : 16'bz;  // Controlled_Buffer controlled_buffer_1
  assign controlled_buffer_2_out = SetMem ? ual_1_p5 : 16'bz;  // Controlled_Buffer controlled_buffer_2
  Pull_Resistor pull_resistor_2 (.node(controlled_buffer_1_out));
  Hex_Digit_Display hex_digit_display_1 (.value(binarytobcd_1_p2));  // open: dp
  Register #(.width(16)) RO0 (.D(controlled_buffer_2_out), .en(SetMem), .Q(RO0_q), .clk(Clk), .clr(Clear));
  Hex_Digit_Display hex_digit_display_2 (.value(binarytobcd_1_p3));  // open: dp
  Hex_Digit_Display hex_digit_display_3 (.value(binarytobcd_1_p4));  // open: dp
  // BinaryToBCD binarytobcd_1: pin names not known; wires that end beside it: RO0_q, binarytobcd_1_p2, binarytobcd_1_p3, binarytobcd_1_p4, binarytobcd_1_p5, binarytobcd_1_p6
  assign controlled_buffer_3_out = SetA ? ual_1_p5 : 16'bz;  // Controlled_Buffer controlled_buffer_3
  Hex_Digit_Display hex_digit_display_4 (.value(binarytobcd_1_p5));  // open: dp
  Hex_Digit_Display hex_digit_display_5 (.value(binarytobcd_1_p6));  // open: dp
  assign pull_resistor_1_node = ReadA ? A_q : 16'bz;  // Controlled_Buffer controlled_buffer_4
  Register #(.width(16)) A (.D(controlled_buffer_3_out), .en(SetA), .Q(A_q), .clk(Clk), .clr(Clear));
  assign controlled_buffer_5_out = SetB ? ual_1_p5 : 16'bz;  // Controlled_Buffer controlled_buffer_5
  assign controlled_buffer_1_out = ReadB ? B_q : 16'bz;  // Controlled_Buffer controlled_buffer_6
  Register #(.width(16)) B (.D(controlled_buffer_5_out), .en(SetB), .Q(B_q), .clk(Clk), .clr(Clear));
  Button button_1 (.out(Clear));
  Clock clock_1 (.out(Clk));
  // UAL ual_1: pin names not known; wires that end beside it: UAL[1], pull_resistor_1_node, UAL[2], UAL[3], ual_1_p5, controlled_buffer_1_out, S___0

  // Notes on the sheet:
  //   Bus Données
  //   Bus B
  //   Bus A
  //   Signaux de contrôle
  //   Bus S
endmodule
