// Logisim project premier_chemin.circ as structural Verilog: 1 circuit, main circuit main
module main (
  input  [3:0] UAL,
  input  SetB,
  input  ReadB,
  input  SetA,
  input  ReadA,
  input  SetPC,
  input  ReadPC,
  input  SetRADM,
  input  SetMem,
  input  ReadMem,
  output S___0
);

  wire Clear, Clk;
  wire [15:0] A_q, B_q, controlled_buffer_1_out, controlled_buffer_2_out, controlled_buffer_3_out,
       controlled_buffer_5_out, controlled_buffer_6_out, controlled_buffer_8_out, controlled_buffer_10_out,
       PC_q, pull_resistor_1_node, ram_1_data, ual_1_p5;

  assign controlled_buffer_1_out = SetMem ? controlled_buffer_2_out : 16'bz;  // Controlled_Buffer controlled_buffer_1
  RAM #(.addrWidth(16), .dataWidth(16), .bus("separate")) ram_1 (
    .addr(controlled_buffer_2_out), .din(controlled_buffer_1_out), .data(ram_1_data), .str(SetMem),
    .clk(Clk), .ld(ReadMem));  // open: sel, clr
  assign controlled_buffer_2_out = ReadMem ? ram_1_data : 16'bz;  // Controlled_Buffer controlled_buffer_2
  assign controlled_buffer_3_out = ReadMem ? controlled_buffer_2_out : 16'bz;  // Controlled_Buffer controlled_buffer_3
  assign controlled_buffer_2_out = SetMem ? ual_1_p5 : 16'bz;  // Controlled_Buffer controlled_buffer_4
  Pull_Resistor pull_resistor_1 (.node(pull_resistor_1_node));
  Pull_Resistor pull_resistor_2 (.node(controlled_buffer_3_out));
  assign controlled_buffer_5_out = SetRADM ? ual_1_p5 : 16'bz;  // Controlled_Buffer controlled_buffer_5
  Register #(.width(16)) Radm (
    .D(controlled_buffer_5_out), .en(SetRADM), .Q(controlled_buffer_2_out), .clk(Clk), .clr(Clear));
  assign controlled_buffer_6_out = SetA ? ual_1_p5 : 16'bz;  // Controlled_Buffer controlled_buffer_6
  Register #(.width(16)) A (.D(controlled_buffer_6_out), .en(SetA), .Q(A_q), .clk(Clk), .clr(Clear));
  assign pull_resistor_1_node = ReadA ? A_q : 16'bz;  // Controlled_Buffer controlled_buffer_7
  assign controlled_buffer_8_out = SetB ? ual_1_p5 : 16'bz;  // Controlled_Buffer controlled_buffer_8
  assign controlled_buffer_3_out = ReadB ? B_q : 16'bz;  // Controlled_Buffer controlled_buffer_9
  Register #(.width(16)) B (.D(controlled_buffer_8_out), .en(SetB), .Q(B_q), .clk(Clk), .clr(Clear));
  assign controlled_buffer_10_out = SetPC ? ual_1_p5 : 16'bz;  // Controlled_Buffer controlled_buffer_10
  Register #(.width(16)) PC (.D(controlled_buffer_10_out), .en(SetPC), .Q(PC_q), .clk(Clk), .clr(Clear));
  assign pull_resistor_1_node = ReadPC ? PC_q : 16'bz;  // Controlled_Buffer controlled_buffer_11
  Button button_1 (.out(Clear));
  Clock clock_1 (.out(Clk));
  // UAL ual_1: pin names not known; wires that end beside it: UAL[1], pull_resistor_1_node, UAL[2], UAL[3], ual_1_p5, controlled_buffer_3_out, S___0

  // Notes on the sheet:
  //   Bus B
  //   Bus A
  //   Bus S
endmodule
