// Logisim project UAL.circ as structural Verilog: 1 circuit, main circuit UAL
module UAL (
  input  [3:0] Code_UAL,
  input  [15:0] A,
  input  [15:0] B,
  output Z,
  output V,
  output [15:0] S,
  output C
);

  wire C0, C1, C2, C3, comparator_1_eq, demultiplexer_1_out0, demultiplexer_1_out1, demultiplexer_1_out2,
       demultiplexer_1_out3, demultiplexer_1_out4, demultiplexer_1_out5, demultiplexer_1_out11;
  wire [15:0] adder_1_out, adder_2_out, and_1_out, C4, multiplier_1_out, not_1_out, not_2_out, or_1_out,
       shifter_1_out, subtractor_1_out, subtractor_2_out;

  assign and_1_out = A & B;  // AND_Gate and_1, 16 bits wide
  assign or_1_out = A | B;  // OR_Gate or_1, 16 bits wide
  assign not_1_out = ~A;  // NOT_Gate not_1, 16 bits wide
  assign not_2_out = ~B;  // NOT_Gate not_2, 16 bits wide
  Adder #(.width(16)) adder_1 (.a(A), .b(B), .out(adder_1_out), .cout(C0));  // open: cin
  Subtractor #(.width(16)) subtractor_1 (.a(A), .b(B), .out(subtractor_1_out), .bout(C1));  // open: bin
  Adder #(.width(16)) adder_2 (.a(A), .b({16{1'b0}}), .out(adder_2_out), .cin(1'b1), .cout(C2));
  Subtractor #(.width(16)) subtractor_2 (.a(A), .b(16'h1), .out(subtractor_2_out), .bout(C3));  // open: bin
  Multiplier #(.width(16)) multiplier_1 (.a(A), .b(B), .out(multiplier_1_out), .cout(C4));  // open: cin
  Shifter #(.shift("lr"), .width(16)) shifter_1 (.in(A), .\dist (4'b0001), .out(shifter_1_out));
  Multiplexer #(.select(4), .width(16)) multiplexer_1 (
    .in0(A), .in1(B), .in2(and_1_out), .in3(or_1_out), .in4(not_1_out), .in5(not_2_out), .in6(adder_1_out),
    .in7(subtractor_1_out), .in8(adder_2_out), .in9(subtractor_2_out), .in10(multiplier_1_out),
    .in11(shifter_1_out), .out(S), .sel(Code_UAL));  // open: in12, in13, in14, in15
  Comparator #(.width(16)) comparator_1 (.a(C4), .b({16{1'b0}}), .eq(comparator_1_eq));  // open: gt, lt
  Comparator #(.mode("unsigned"), .width(16)) comparator_2 (.a({16{1'b0}}), .b(S), .eq(Z));  // open: gt, lt
  Demultiplexer #(.select(4)) demultiplexer_1 (
    .out0(demultiplexer_1_out0), .out1(demultiplexer_1_out1), .out2(demultiplexer_1_out2),
    .out3(demultiplexer_1_out3), .out4(demultiplexer_1_out4), .out5(demultiplexer_1_out5), .out6(C0),
    .out7(C1), .out8(C2), .out9(C3), .out10(comparator_1_eq), .out11(demultiplexer_1_out11), .in(C));  // open: out12, out13, out14, out15, sel
  // also tied to GND on the sheet: {demultiplexer_1_out0, demultiplexer_1_out1, demultiplexer_1_out2, demultiplexer_1_out3, demultiplexer_1_out4, demultiplexer_1_out5, demultiplexer_1_out11}
endmodule
