// Logisim project archi_all.circ as structural Verilog: 7 circuits, main circuit main
module main (
);

  wire and_1_out, and_2_out, and_3_out, and_4_out, and_5_out, and_6_out, Clear, ClearIF, clk,
       comparator_1_eq, comparator_2_eq, comparator_3_eq, IFlag, INTA, INTR, not_1_out, or_1_out, ReadA,
       ReadB, ReadINTAddr, ReadMem, ReadPC, ReadSP, regselect_1_enabled, SetA, SetB, SetIF, SetMem, SetPC,
       SetRADM, SetSP, Z;
  wire [1:0] MuxSel_smux;
  wire [2:0] CodeMCount;
  wire [3:0] binarytobcd_circ_1_d0, binarytobcd_circ_1_d1, binarytobcd_circ_1_d2, binarytobcd_circ_1_d3,
       binarytobcd_circ_1_d4, binarytobcd_circ_2_d0, binarytobcd_circ_2_d1, binarytobcd_circ_2_d2,
       binarytobcd_circ_2_d3, binarytobcd_circ_2_d4, binarytobcd_circ_3_d0, binarytobcd_circ_3_d1,
       binarytobcd_circ_3_d2, binarytobcd_circ_3_d3, binarytobcd_circ_3_d4, Code_UAL;
  wire [6:0] keyboard_1_data, register_1_q;
  wire [7:0] adder_1_out, JMP_Adr, MicroPC_q, multiplexer_1_out, pull_resistor_2_node, pull_resistor_2_node_2;
  wire [15:0] A_q, AddrBus, B_q, controlled_buffer_1_out, controlled_buffer_4_out, controlled_buffer_5_out,
       controlled_buffer_8_out, controlled_buffer_10_out, controlled_buffer_12_out, controlled_buffer_14_out,
       controlled_buffer_15_out, controlled_buffer_17_out, DBus, graphiccard_1_p7, graphiccard_1_p8,
       graphiccard_1_p9, graphiccard_1_p10, graphiccard_1_p11, graphiccard_1_p12, graphiccard_1_p13,
       graphiccard_1_p14, graphiccard_1_p15, graphiccard_1_p16, graphiccard_1_p17, graphiccard_1_p18,
       graphiccard_1_p19, graphiccard_1_p20, graphiccard_1_p21, graphiccard_1_p22, MainMemory_dout, PC_q,
       pull_resistor_1_node, register_2_q, register_3_q, register_5_q, regselect_1_dataout, SP_q, ual_1_p3;
  wire [31:30] Sequencer_data;

  Button Reset (.out(Clear));
  Clock clock_1 (.out(clk));
  not not_1 (not_1_out, AddrBus[12]);
  LED MemSelected (.in(not_1_out));
  assign controlled_buffer_1_out = and_1_out ? DBus : 16'bz;  // Controlled_Buffer controlled_buffer_1
  and and_1 (and_1_out, SetMem, not_1_out);
  and and_2 (and_2_out, ReadMem, not_1_out);
  RAM #(.addrWidth(16), .dataWidth(16), .trigger("falling")) MainMemory (
    .addr(AddrBus), .we(and_1_out), .oe(and_2_out), .clk(clk), .din(controlled_buffer_1_out),
    .dout(MainMemory_dout));
  Comparator #(.mode("unsigned"), .width(16)) comparator_1 (
    .a(AddrBus), .b(16'h1000), .eq(comparator_1_eq));  // open: gt, lt
  Pull_Resistor pull_resistor_1 (.node(pull_resistor_1_node));
  Pull_Resistor pull_resistor_2 (.node({pull_resistor_2_node_2, pull_resistor_2_node}));
  assign {pull_resistor_2_node_2, pull_resistor_2_node} = ReadMem ? DBus : 16'bz;  // Controlled_Buffer controlled_buffer_2
  assign DBus = SetMem ? ual_1_p3 : 16'bz;  // Controlled_Buffer controlled_buffer_3
  Keyboard #(.buflen(1)) keyboard_1 (.clk(clk), .re(INTA), .clr(Clear), .avail(INTR), .data(keyboard_1_data));
  and and_3 (and_3_out, SetMem, comparator_1_eq);
  assign controlled_buffer_4_out = and_3_out ? DBus : 16'bz;  // Controlled_Buffer controlled_buffer_4
  assign controlled_buffer_5_out = SetRADM ? ual_1_p3 : 16'bz;  // Controlled_Buffer controlled_buffer_5
  assign DBus = and_2_out ? MainMemory_dout : 16'bz;  // Controlled_Buffer controlled_buffer_6
  Register #(.width(16)) Radm (.D(controlled_buffer_5_out), .en(SetRADM), .clk(clk), .Q(AddrBus), .clr(Clear));
  Register #(.width(7)) register_1 (.D(keyboard_1_data), .en(INTA), .clk(INTA), .Q(register_1_q), .clr(Clear));
  Register #(.width(16)) register_2 (
    .D(controlled_buffer_4_out), .en(and_3_out), .clk(clk), .Q(register_2_q), .clr(Clear));
  assign pull_resistor_1_node = ReadINTAddr ? 16'h2 : 16'bz;  // Controlled_Buffer controlled_buffer_7
  assign controlled_buffer_8_out = SetA ? ual_1_p3 : 16'bz;  // Controlled_Buffer controlled_buffer_8
  Hex_Digit_Display Hex_Digit_Display_1 (.value(binarytobcd_circ_1_d4));  // open: dp
  BinaryToBCD_circ binarytobcd_circ_1 (
    .Input_bus_1(register_2_q), .D4(binarytobcd_circ_1_d4), .D3(binarytobcd_circ_1_d3),
    .D2(binarytobcd_circ_1_d2), .D1(binarytobcd_circ_1_d1), .D0(binarytobcd_circ_1_d0));
  Register #(.width(16)) A (.D(controlled_buffer_8_out), .en(SetA), .clk(clk), .Q(A_q), .clr(Clear));
  Hex_Digit_Display Hex_Digit_Display_3 (.value(binarytobcd_circ_1_d2));  // open: dp
  Hex_Digit_Display Hex_Digit_Display_2 (.value(binarytobcd_circ_1_d3));  // open: dp
  assign pull_resistor_1_node = ReadA ? A_q : 16'bz;  // Controlled_Buffer controlled_buffer_9
  Hex_Digit_Display Hex_Digit_Display_4 (.value(binarytobcd_circ_1_d1));  // open: dp
  Hex_Digit_Display Hex_Digit_Display_5 (.value(binarytobcd_circ_1_d0));  // open: dp
  Adder adder_1 (.a(MicroPC_q), .b(8'h1), .out(adder_1_out));  // open: cin, cout
  Register #(.width(16)) B (.D(controlled_buffer_10_out), .en(SetB), .clk(clk), .Q(B_q), .clr(Clear));
  assign controlled_buffer_10_out = SetB ? ual_1_p3 : 16'bz;  // Controlled_Buffer controlled_buffer_10
  RegSelect KeyRegSelect (
    .Enable(ReadMem), .Addr(16'h1003), .AddrBus(AddrBus), .DataBus({{9{1'b0}}, register_1_q}), .DataOut(DBus));  // open: Enabled
  Multiplexer #(.select(2), .width(8)) multiplexer_1 (
    .in0(adder_1_out), .in1(JMP_Adr), .in2(pull_resistor_2_node_2), .out(multiplexer_1_out), .sel(MuxSel_smux));  // open: in3
  MuxSelOpt MuxSel (.CodeMCount(CodeMCount), .Z(Z), .INTR_IF(and_4_out), .SMux(MuxSel_smux));
  and and_4 (and_4_out, IFlag, INTR);
  assign {pull_resistor_2_node_2, pull_resistor_2_node} = ReadB ? B_q : 16'bz;  // Controlled_Buffer controlled_buffer_11
  Register #(.width(16)) PC (.D(controlled_buffer_12_out), .en(SetPC), .clk(clk), .Q(PC_q), .clr(Clear));
  assign controlled_buffer_12_out = SetPC ? ual_1_p3 : 16'bz;  // Controlled_Buffer controlled_buffer_12
  Comparator #(.mode("unsigned"), .width(16)) comparator_2 (
    .a(AddrBus), .b(16'h1001), .eq(comparator_2_eq));  // open: gt, lt
  Register MicroPC (.D(multiplexer_1_out), .en(1'b1), .clk(clk), .Q(MicroPC_q), .clr(Clear));
  assign pull_resistor_1_node = ReadPC ? PC_q : 16'bz;  // Controlled_Buffer controlled_buffer_13
  and and_5 (and_5_out, SetMem, comparator_2_eq);
  assign controlled_buffer_14_out = and_5_out ? DBus : 16'bz;  // Controlled_Buffer controlled_buffer_14
  assign controlled_buffer_15_out = SetSP ? ual_1_p3 : 16'bz;  // Controlled_Buffer controlled_buffer_15
  Register #(.width(16)) SP (.D(controlled_buffer_15_out), .en(SetSP), .clk(clk), .Q(SP_q), .clr(Clear));
  // GraphicCard graphiccard_1: pin names not known; wires that end beside it: AddrBus, DBus, clk, SetMem, Clear, 16'h2000, graphiccard_1_p7, graphiccard_1_p8, graphiccard_1_p9, graphiccard_1_p10, graphiccard_1_p11, graphiccard_1_p12, graphiccard_1_p13, graphiccard_1_p14, graphiccard_1_p15, graphiccard_1_p16, graphiccard_1_p17, graphiccard_1_p18, graphiccard_1_p19, graphiccard_1_p20, graphiccard_1_p21, graphiccard_1_p22
  Register #(.width(16)) register_3 (
    .D(controlled_buffer_14_out), .en(and_5_out), .clk(clk), .Q(register_3_q), .clr(Clear));
  assign pull_resistor_1_node = ReadSP ? SP_q : 16'bz;  // Controlled_Buffer controlled_buffer_16
  DotMatrix #(.inputtype("row"), .matrixcols(16), .matrixrows(16)) Screen (
    .row0(graphiccard_1_p7), .row1(graphiccard_1_p8), .row2(graphiccard_1_p9), .row3(graphiccard_1_p10),
    .row4(graphiccard_1_p11), .row5(graphiccard_1_p12), .row6(graphiccard_1_p13), .row7(graphiccard_1_p14),
    .row8(graphiccard_1_p15), .row9(graphiccard_1_p16), .row10(graphiccard_1_p17), .row11(graphiccard_1_p18),
    .row12(graphiccard_1_p19), .row13(graphiccard_1_p20), .row14(graphiccard_1_p21), .row15(graphiccard_1_p22));
  ROM #(.dataWidth(32)) Sequencer (
    .addr(MicroPC_q),
    .data({Sequencer_data, ReadINTAddr, ClearIF, SetIF, INTA, CodeMCount, Code_UAL, SetSP, ReadSP, SetB, ReadB, SetA, ReadA, SetPC, ReadPC, SetRADM, SetMem, ReadMem, JMP_Adr}));
  Hex_Digit_Display hex_digit_display_1_dup2 (.value(binarytobcd_circ_2_d4));  // open: dp
  BinaryToBCD_circ binarytobcd_circ_2 (
    .Input_bus_1(register_3_q), .D4(binarytobcd_circ_2_d4), .D3(binarytobcd_circ_2_d3),
    .D2(binarytobcd_circ_2_d2), .D1(binarytobcd_circ_2_d1), .D0(binarytobcd_circ_2_d0));
  Hex_Digit_Display hex_digit_display_2_dup2 (.value(binarytobcd_circ_2_d3));  // open: dp
  Hex_Digit_Display hex_digit_display_3_dup2 (.value(binarytobcd_circ_2_d2));  // open: dp
  or or_1 (or_1_out, ClearIF, SetIF);
  Hex_Digit_Display hex_digit_display_4_dup2 (.value(binarytobcd_circ_2_d1));  // open: dp
  Hex_Digit_Display hex_digit_display_5_dup2 (.value(binarytobcd_circ_2_d0));  // open: dp
  Register #(.width(1)) register_4 (.D(SetIF), .en(or_1_out), .clk(clk), .Q(IFlag), .clr(Clear));
  RegSelect regselect_1 (
    .Enable(SetMem), .Addr(16'h1004), .AddrBus(AddrBus), .DataBus(DBus), .DataOut(regselect_1_dataout),
    .Enabled(regselect_1_enabled));
  and and_6 (and_6_out, SetMem, comparator_3_eq);
  Comparator #(.mode("unsigned"), .width(16)) comparator_3 (
    .a(AddrBus), .b(16'h1002), .eq(comparator_3_eq));  // open: gt, lt
  assign controlled_buffer_17_out = and_6_out ? DBus : 16'bz;  // Controlled_Buffer controlled_buffer_17
  TTY tty_1 (.data(regselect_1_dataout[6:0]), .clk(clk), .we(regselect_1_enabled), .clr(Clear));
  Register #(.width(16)) register_5 (
    .D(controlled_buffer_17_out), .en(and_6_out), .clk(clk), .Q(register_5_q), .clr(Clear));
  // UAL ual_1: pin names not known; wires that end beside it: Code_UAL, pull_resistor_1_node, ual_1_p3, {pull_resistor_2_node_2, pull_resistor_2_node}, Z
  Hex_Digit_Display hex_digit_display_6 (.value(binarytobcd_circ_3_d4));  // open: dp
  Hex_Digit_Display hex_digit_display_7 (.value(binarytobcd_circ_3_d3));  // open: dp
  BinaryToBCD_circ binarytobcd_circ_3 (
    .Input_bus_1(register_5_q), .D4(binarytobcd_circ_3_d4), .D3(binarytobcd_circ_3_d3),
    .D2(binarytobcd_circ_3_d2), .D1(binarytobcd_circ_3_d1), .D0(binarytobcd_circ_3_d0));
  Hex_Digit_Display hex_digit_display_8 (.value(binarytobcd_circ_3_d2));  // open: dp
  Hex_Digit_Display hex_digit_display_9 (.value(binarytobcd_circ_3_d1));  // open: dp
  Hex_Digit_Display hex_digit_display_10 (.value(binarytobcd_circ_3_d0));  // open: dp

  // Notes on the sheet:
  //   Is the memory selected ?
  //   Bus B
  //   Bus A
  //   contents of Sequencer (hex, n*v repeats v):
  //   2000008 8000e0 6*0 c00 1401900 0 0 80000c 0 0 0 c00 84100 c01800 0 c00 80500 84100 c01800 88400
  //   802200 0 0 c00 80500 2200 c01800 c00 90100 c01800 0 c00 80500 90100 c01800 2400 888200 0 0 c00 80500
  //   8a200 c01800 b0e000 0 0 0 b1a000 0 0 0 b8e000 0 0 0 b9a000 0 0 0 d0e000 0 0 0 d1a000 0 0 0 d86000
  //   7*0 90e000 0 0 0 91a000 0 0 0 98e000 0 0 0 99a000 0 0 0 a06000 0 0 0 a98000 11*0 c00 881100 0 0
  //   1802076 c01800 c00 881100 188807a c01800 c00 881100 4*0 c00 c0100 c01800 0 c00 80500 c0100 c01800
  //   4*0 c00 80500 20200 c01800 c60000 0 0 0 ce0000 11*0 20400 400a00 4e0000 c00 881100 0 0 0 460400
  //   881100 6*0 20400 2200 ce0000 0 460400 884100 0 0 c00 320500 2200 c01800 c00 320500 84100 c01800
  //   20400 88200 ce0000 0 460400 890100 0 0 c00 320500 88200 c01800 c00 320500 90100 c01800 10800000 0 0
  //   0 8800000 11*0 14020400 2200 4e0400 88200 4e0400 a00 4e0000 20801008 460400 81100 460400 90100
  //   460400 8884100
  //   S = 0 ?
endmodule

module MuxSelOpt (
  input  [2:0] CodeMCount,
  input  Z,
  input  INTR_IF,
  output [1:0] SMux
);

  wire and_2_out, and_3_out, and_4_out, not_1_out, not_2_out, not_3_out;

  not not_1 (not_1_out, CodeMCount[1]);
  not not_2 (not_2_out, CodeMCount[0]);
  not not_3 (not_3_out, INTR_IF);
  and and_1 (SMux[1], CodeMCount[1], not_2_out);
  and and_2 (and_2_out, not_1_out, CodeMCount[0]);
  and and_3 (and_3_out, CodeMCount[0], Z);
  and and_4 (and_4_out, CodeMCount[2], not_3_out);
  or or_1 (SMux[0], and_2_out, and_3_out, and_4_out);
endmodule

module Add3 (
  input  A3,
  input  A2,
  input  A1,
  input  A0,
  output S3,
  output S2,
  output S1,
  output S0
);

  wire and_1_out, and_2_out, and_3_out, and_4_out, and_5_out, and_6_out, and_7_out, and_8_out, and_9_out,
       and_10_out, not_1_out, not_2_out, not_3_out, not_4_out;

  not not_1 (not_1_out, A3);
  not not_2 (not_2_out, A2);
  not not_3 (not_3_out, A1);
  not not_4 (not_4_out, A0);
  and and_1 (and_1_out, A2, A0);
  and and_2 (and_2_out, A2, A1);
  and and_3 (and_3_out, A2, not_3_out, not_4_out);
  and and_4 (and_4_out, A3, A0);
  and and_5 (and_5_out, not_2_out, A1);
  and and_6 (and_6_out, A1, A0);
  and and_7 (and_7_out, A3, not_4_out);
  and and_8 (and_8_out, not_1_out, not_2_out, A0);
  and and_9 (and_9_out, A2, A1, not_4_out);
  and and_10 (and_10_out, A3, not_4_out);
  or or_1 (S3, and_1_out, and_2_out, A3);
  or or_2 (S2, and_3_out, and_4_out);
  or or_3 (S1, and_5_out, and_6_out, and_7_out);
  or or_4 (S0, and_8_out, and_9_out, and_10_out);
endmodule

module BinaryToBCD_circ (
  input  [15:0] Input_bus_1,
  output [3:0] D4,
  output [3:0] D3,
  output [3:0] D2,
  output [3:0] D1,
  output [3:0] D0
);

  wire Add3_1_s0, Add3_1_s1, Add3_1_s2, Add3_1_s3, Add3_2_s0, Add3_2_s1, Add3_2_s2, Add3_2_s3, Add3_3_s0,
       Add3_3_s1, Add3_3_s2, Add3_3_s3, Add3_4_s0, Add3_4_s1, Add3_4_s2, Add3_4_s3, Add3_5_s0, Add3_5_s1,
       Add3_5_s2, Add3_5_s3, Add3_6_s0, Add3_6_s1, Add3_6_s2, Add3_6_s3, Add3_7_s0, Add3_7_s1, Add3_7_s2,
       Add3_7_s3, Add3_8_s0, Add3_8_s1, Add3_8_s2, Add3_8_s3, Add3_9_s0, Add3_9_s1, Add3_9_s2, Add3_9_s3,
       Add3_10_s0, Add3_10_s1, Add3_10_s2, Add3_10_s3, Add3_11_s0, Add3_11_s1, Add3_11_s2, Add3_11_s3,
       Add3_12_s0, Add3_12_s1, Add3_12_s2, Add3_12_s3, Add3_13_s0, Add3_13_s1, Add3_13_s2, Add3_13_s3,
       Add3_14_s0, Add3_14_s1, Add3_14_s2, Add3_14_s3, Add3_15_s0, Add3_15_s1, Add3_15_s2, Add3_15_s3,
       Add3_16_s0, Add3_16_s1, Add3_16_s2, Add3_16_s3, Add3_17_s0, Add3_17_s1, Add3_17_s2, Add3_17_s3,
       Add3_18_s0, Add3_18_s1, Add3_18_s2, Add3_18_s3, Add3_19_s0, Add3_19_s1, Add3_19_s2, Add3_19_s3,
       Add3_20_s0, Add3_20_s1, Add3_20_s2, Add3_20_s3, Add3_21_s0, Add3_21_s1, Add3_21_s2, Add3_21_s3,
       Add3_22_s0, Add3_22_s1, Add3_22_s2, Add3_22_s3, Add3_23_s0, Add3_23_s1, Add3_23_s2, Add3_23_s3,
       Add3_24_s0, Add3_24_s1, Add3_24_s2, Add3_24_s3, Add3_25_s0, Add3_25_s1, Add3_25_s2, Add3_25_s3,
       Add3_26_s0, Add3_26_s1, Add3_26_s2, Add3_26_s3, Add3_27_s0, Add3_27_s1, Add3_27_s2, Add3_27_s3,
       Add3_28_s0, Add3_28_s1, Add3_28_s2, Add3_28_s3, Add3_29_s0, Add3_29_s1, Add3_29_s2, Add3_29_s3,
       Add3_30_s0, Add3_30_s1, Add3_30_s2, Add3_30_s3;

  Add3 Add3_31 (
    .A0(Add3_27_s3), .A3(1'b0), .A2(Add3_19_s3), .A1(Add3_23_s3), .S2(D4[3]), .S1(D4[2]), .S0(D4[1]));  // open: S3
  Add3 Add3_1 (
    .A0(Input_bus_1[13]), .A3(1'b0), .A2(Input_bus_1[15]), .A1(Input_bus_1[14]), .S3(Add3_1_s3),
    .S2(Add3_1_s2), .S1(Add3_1_s1), .S0(Add3_1_s0));
  Add3 Add3_4 (
    .A0(Add3_3_s3), .A3(1'b0), .A2(Add3_1_s3), .A1(Add3_2_s3), .S3(Add3_4_s3), .S2(Add3_4_s2),
    .S1(Add3_4_s1), .S0(Add3_4_s0));
  Add3 Add3_6 (
    .A0(Add3_5_s3), .A3(Add3_4_s2), .A2(Add3_4_s1), .A1(Add3_4_s0), .S3(Add3_6_s3), .S2(Add3_6_s2),
    .S1(Add3_6_s1), .S0(Add3_6_s0));
  Add3 Add3_10 (
    .A0(Add3_8_s3), .A3(1'b0), .A2(Add3_4_s3), .A1(Add3_6_s3), .S3(Add3_10_s3), .S2(Add3_10_s2),
    .S1(Add3_10_s1), .S0(Add3_10_s0));
  Add3 Add3_13 (
    .A0(Add3_11_s3), .A3(Add3_10_s2), .A2(Add3_10_s1), .A1(Add3_10_s0), .S3(Add3_13_s3), .S2(Add3_13_s2),
    .S1(Add3_13_s1), .S0(Add3_13_s0));
  Add3 Add3_16 (
    .A0(Add3_14_s3), .A3(Add3_13_s2), .A2(Add3_13_s1), .A1(Add3_13_s0), .S3(Add3_16_s3), .S2(Add3_16_s2),
    .S1(Add3_16_s1), .S0(Add3_16_s0));
  Add3 Add3_19 (
    .A0(Add3_16_s3), .A3(1'b0), .A2(Add3_10_s3), .A1(Add3_13_s3), .S3(Add3_19_s3), .S2(Add3_19_s2),
    .S1(Add3_19_s1), .S0(Add3_19_s0));
  Add3 Add3_23 (
    .A0(Add3_20_s3), .A3(Add3_19_s2), .A2(Add3_19_s1), .A1(Add3_19_s0), .S3(Add3_23_s3), .S2(Add3_23_s2),
    .S1(Add3_23_s1), .S0(Add3_23_s0));
  Add3 Add3_27 (
    .A0(Add3_24_s3), .A3(Add3_23_s2), .A2(Add3_23_s1), .A1(Add3_23_s0), .S3(Add3_27_s3), .S2(Add3_27_s2),
    .S1(Add3_27_s1), .S0(Add3_27_s0));
  Add3 Add3_32 (
    .A0(Add3_28_s3), .A3(Add3_27_s2), .A2(Add3_27_s1), .A1(Add3_27_s0), .S3(D4[0]), .S2(D3[3]), .S1(D3[2]),
    .S0(D3[1]));
  Add3 Add3_2 (
    .A0(Input_bus_1[12]), .A3(Add3_1_s2), .A2(Add3_1_s1), .A1(Add3_1_s0), .S3(Add3_2_s3), .S2(Add3_2_s2),
    .S1(Add3_2_s1), .S0(Add3_2_s0));
  Add3 Add3_3 (
    .A0(Input_bus_1[11]), .A3(Add3_2_s2), .A2(Add3_2_s1), .A1(Add3_2_s0), .S3(Add3_3_s3), .S2(Add3_3_s2),
    .S1(Add3_3_s1), .S0(Add3_3_s0));
  Add3 Add3_5 (
    .A0(Input_bus_1[10]), .A3(Add3_3_s2), .A2(Add3_3_s1), .A1(Add3_3_s0), .S3(Add3_5_s3), .S2(Add3_5_s2),
    .S1(Add3_5_s1), .S0(Add3_5_s0));
  Add3 Add3_7 (
    .A0(Input_bus_1[9]), .A3(Add3_5_s2), .A2(Add3_5_s1), .A1(Add3_5_s0), .S3(Add3_7_s3), .S2(Add3_7_s2),
    .S1(Add3_7_s1), .S0(Add3_7_s0));
  Add3 Add3_8 (
    .A0(Add3_7_s3), .A3(Add3_6_s2), .A2(Add3_6_s1), .A1(Add3_6_s0), .S3(Add3_8_s3), .S2(Add3_8_s2),
    .S1(Add3_8_s1), .S0(Add3_8_s0));
  Add3 Add3_11 (
    .A0(Add3_9_s3), .A3(Add3_8_s2), .A2(Add3_8_s1), .A1(Add3_8_s0), .S3(Add3_11_s3), .S2(Add3_11_s2),
    .S1(Add3_11_s1), .S0(Add3_11_s0));
  Add3 Add3_14 (
    .A0(Add3_12_s3), .A3(Add3_11_s2), .A2(Add3_11_s1), .A1(Add3_11_s0), .S3(Add3_14_s3), .S2(Add3_14_s2),
    .S1(Add3_14_s1), .S0(Add3_14_s0));
  Add3 Add3_17 (
    .A0(Add3_15_s3), .A3(Add3_14_s2), .A2(Add3_14_s1), .A1(Add3_14_s0), .S3(Add3_17_s3), .S2(Add3_17_s2),
    .S1(Add3_17_s1), .S0(Add3_17_s0));
  Add3 Add3_20 (
    .A0(Add3_17_s3), .A3(Add3_16_s2), .A2(Add3_16_s1), .A1(Add3_16_s0), .S3(Add3_20_s3), .S2(Add3_20_s2),
    .S1(Add3_20_s1), .S0(Add3_20_s0));
  Add3 Add3_24 (
    .A0(Add3_21_s3), .A3(Add3_20_s2), .A2(Add3_20_s1), .A1(Add3_20_s0), .S3(Add3_24_s3), .S2(Add3_24_s2),
    .S1(Add3_24_s1), .S0(Add3_24_s0));
  Add3 Add3_28 (
    .A0(Add3_25_s3), .A3(Add3_24_s2), .A2(Add3_24_s1), .A1(Add3_24_s0), .S3(Add3_28_s3), .S2(Add3_28_s2),
    .S1(Add3_28_s1), .S0(Add3_28_s0));
  Add3 Add3_33 (
    .A0(Add3_29_s3), .A3(Add3_28_s2), .A2(Add3_28_s1), .A1(Add3_28_s0), .S3(D3[0]), .S2(D2[3]), .S1(D2[2]),
    .S0(D2[1]));
  Add3 Add3_9 (
    .A0(Input_bus_1[8]), .A3(Add3_7_s2), .A2(Add3_7_s1), .A1(Add3_7_s0), .S3(Add3_9_s3), .S2(Add3_9_s2),
    .S1(Add3_9_s1), .S0(Add3_9_s0));
  Add3 Add3_12 (
    .A0(Input_bus_1[7]), .A3(Add3_9_s2), .A2(Add3_9_s1), .A1(Add3_9_s0), .S3(Add3_12_s3), .S2(Add3_12_s2),
    .S1(Add3_12_s1), .S0(Add3_12_s0));
  Add3 Add3_15 (
    .A0(Input_bus_1[6]), .A3(Add3_12_s2), .A2(Add3_12_s1), .A1(Add3_12_s0), .S3(Add3_15_s3), .S2(Add3_15_s2),
    .S1(Add3_15_s1), .S0(Add3_15_s0));
  Add3 Add3_18 (
    .A0(Input_bus_1[5]), .A3(Add3_15_s2), .A2(Add3_15_s1), .A1(Add3_15_s0), .S3(Add3_18_s3), .S2(Add3_18_s2),
    .S1(Add3_18_s1), .S0(Add3_18_s0));
  Add3 Add3_21 (
    .A0(Add3_18_s3), .A3(Add3_17_s2), .A2(Add3_17_s1), .A1(Add3_17_s0), .S3(Add3_21_s3), .S2(Add3_21_s2),
    .S1(Add3_21_s1), .S0(Add3_21_s0));
  Add3 Add3_25 (
    .A0(Add3_22_s3), .A3(Add3_21_s2), .A2(Add3_21_s1), .A1(Add3_21_s0), .S3(Add3_25_s3), .S2(Add3_25_s2),
    .S1(Add3_25_s1), .S0(Add3_25_s0));
  Add3 Add3_29 (
    .A0(Add3_26_s3), .A3(Add3_25_s2), .A2(Add3_25_s1), .A1(Add3_25_s0), .S3(Add3_29_s3), .S2(Add3_29_s2),
    .S1(Add3_29_s1), .S0(Add3_29_s0));
  Add3 Add3_34 (
    .A0(Add3_30_s3), .A3(Add3_29_s2), .A2(Add3_29_s1), .A1(Add3_29_s0), .S3(D2[0]), .S2(D1[3]), .S1(D1[2]),
    .S0(D1[1]));
  Add3 Add3_22 (
    .A0(Input_bus_1[4]), .A3(Add3_18_s2), .A2(Add3_18_s1), .A1(Add3_18_s0), .S3(Add3_22_s3), .S2(Add3_22_s2),
    .S1(Add3_22_s1), .S0(Add3_22_s0));
  Add3 Add3_26 (
    .A0(Input_bus_1[3]), .A3(Add3_22_s2), .A2(Add3_22_s1), .A1(Add3_22_s0), .S3(Add3_26_s3), .S2(Add3_26_s2),
    .S1(Add3_26_s1), .S0(Add3_26_s0));
  Add3 Add3_30 (
    .A0(Input_bus_1[2]), .A3(Add3_26_s2), .A2(Add3_26_s1), .A1(Add3_26_s0), .S3(Add3_30_s3), .S2(Add3_30_s2),
    .S1(Add3_30_s1), .S0(Add3_30_s0));
  Add3 Add3_35 (
    .A0(Input_bus_1[1]), .A3(Add3_30_s2), .A2(Add3_30_s1), .A1(Add3_30_s0), .S3(D1[0]), .S2(D0[3]),
    .S1(D0[2]), .S0(D0[1]));

  assign D0[0] = Input_bus_1[0];
endmodule

module RegSelect (
  input  Enable,
  input  [15:0] Addr,
  input  [15:0] AddrBus,
  input  [15:0] DataBus,
  output [15:0] DataOut,
  output Enabled
);

  wire comparator_1_eq;

  Comparator #(.width(16)) comparator_1 (.a(Addr), .b(AddrBus), .eq(comparator_1_eq));  // open: gt, lt
  and and_1 (Enabled, Enable, comparator_1_eq);
  assign DataOut = Enabled ? DataBus : 16'bz;  // Controlled_Buffer controlled_buffer_1
endmodule

module GraphicalCard_circ (
  input  [15:0] AddrBus,
  input  [15:0] DataBus,
  input  SetMem,
  input  Clock,
  input  Clear,
  input  [15:0] BaseAddr,
  output [15:0] R0,
  output [15:0] R1,
  output [15:0] R2,
  output [15:0] R3,
  output [15:0] R4,
  output [15:0] R5,
  output [15:0] R6,
  output [15:0] R7,
  output [15:0] R8,
  output [15:0] R9,
  output [15:0] R10,
  output [15:0] R11,
  output [15:0] R12,
  output [15:0] R13,
  output [15:0] R14,
  output [15:0] R15
);

  wire adder_1_cout, adder_5_cout, adder_9_cout, adder_13_cout, and_1_out, and_2_out, and_3_out, and_4_out,
       and_5_out, and_6_out, and_7_out, and_8_out, and_9_out, and_10_out, and_11_out, and_12_out, and_13_out,
       and_14_out, and_15_out, and_16_out, and_17_out, and_18_out, and_19_out, and_20_out, and_21_out,
       and_22_out, and_23_out, and_24_out, and_25_out, and_26_out, and_27_out, and_28_out, and_29_out,
       and_30_out, and_31_out, and_32_out, BufferSelect, not_1_out, regselect_1_enabled, regselect_2_enabled,
       regselect_3_enabled, regselect_4_enabled, regselect_5_enabled, regselect_6_enabled,
       regselect_7_enabled, regselect_8_enabled, regselect_9_enabled, regselect_10_enabled,
       regselect_11_enabled, regselect_12_enabled, regselect_13_enabled, regselect_14_enabled,
       regselect_15_enabled, regselect_16_enabled, regselect_17_enabled, regselect_18_enabled,
       regselect_19_enabled, regselect_20_enabled, regselect_21_enabled, regselect_22_enabled,
       regselect_23_enabled, regselect_24_enabled, regselect_25_enabled, regselect_26_enabled,
       regselect_27_enabled, regselect_28_enabled, regselect_29_enabled, regselect_30_enabled,
       regselect_31_enabled, regselect_32_enabled, regselect_33_enabled;
  wire [15:0] adder_1_out, adder_2_out, adder_3_out, adder_4_out, adder_5_out, adder_6_out, adder_7_out,
       adder_8_out, adder_9_out, adder_10_out, adder_11_out, adder_12_out, adder_13_out, adder_14_out,
       adder_15_out, adder_16_out, L0, L1, L2, L3, L4, L5, L6, L7, L8, L9, L10, L11, L12, L13, L14, L15, M0,
       M1, M2, M3, M4, M5, M6, M7, M8, M9, M10, M11, M12, M13, M14, M15, regselect_1_dataout,
       regselect_2_dataout, regselect_3_dataout, regselect_4_dataout, regselect_5_dataout,
       regselect_6_dataout, regselect_7_dataout, regselect_8_dataout, regselect_9_dataout,
       regselect_10_dataout, regselect_11_dataout, regselect_12_dataout, regselect_13_dataout,
       regselect_14_dataout, regselect_15_dataout, regselect_16_dataout, regselect_17_dataout,
       regselect_18_dataout, regselect_19_dataout, regselect_20_dataout, regselect_21_dataout,
       regselect_22_dataout, regselect_23_dataout, regselect_24_dataout, regselect_25_dataout,
       regselect_26_dataout, regselect_27_dataout, regselect_28_dataout, regselect_29_dataout,
       regselect_30_dataout, regselect_31_dataout, regselect_32_dataout, regselect_33_dataout;

  Adder #(.width(16)) adder_1 (.a(BaseAddr), .b(16'h1), .out(adder_1_out), .cout(adder_1_cout));  // open: cin
  Adder #(.width(16)) adder_2 (.a(BaseAddr), .b(16'h2), .out(adder_2_out));  // open: cin, cout
  Adder #(.width(16)) adder_3 (.a(BaseAddr), .b(16'h3), .out(adder_3_out));  // open: cin, cout
  Adder #(.width(16)) adder_4 (.a(BaseAddr), .b(16'h4), .out(adder_4_out));  // open: cin, cout
  Adder #(.width(16)) adder_5 (.a(BaseAddr), .b(16'h5), .out(adder_5_out), .cout(adder_5_cout));  // open: cin
  Adder #(.width(16)) adder_6 (.a(BaseAddr), .b(16'h6), .out(adder_6_out));  // open: cin, cout
  Adder #(.width(16)) adder_7 (.a(BaseAddr), .b(16'h7), .out(adder_7_out));  // open: cin, cout
  Adder #(.width(16)) adder_8 (.a(BaseAddr), .b(16'h8), .out(adder_8_out));  // open: cin, cout
  Adder #(.width(16)) adder_9 (.a(BaseAddr), .b(16'h9), .out(adder_9_out), .cout(adder_9_cout));  // open: cin
  Adder #(.width(16)) adder_10 (.a(BaseAddr), .b(16'ha), .out(adder_10_out));  // open: cin, cout
  Adder #(.width(16)) adder_11 (.a(BaseAddr), .b(16'hb), .out(adder_11_out));  // open: cin, cout
  Adder #(.width(16)) adder_12 (.a(BaseAddr), .b(16'hc), .out(adder_12_out));  // open: cin, cout
  Adder #(.width(16)) adder_13 (.a(BaseAddr), .b(16'hd), .out(adder_13_out), .cout(adder_13_cout));  // open: cin
  Adder #(.width(16)) adder_14 (.a(BaseAddr), .b(16'he), .out(adder_14_out));  // open: cin, cout
  Adder #(.width(16)) adder_15 (.a(BaseAddr), .b(16'hf), .out(adder_15_out));  // open: cin, cout
  Adder #(.width(16)) adder_16 (.a(BaseAddr), .b(16'h10), .out(adder_16_out));  // open: cin, cout
  and and_1 (and_1_out, BufferSelect, SetMem);
  and and_2 (and_2_out, BufferSelect, SetMem);
  and and_3 (and_3_out, BufferSelect, SetMem);
  and and_4 (and_4_out, BufferSelect, SetMem);
  and and_5 (and_5_out, BufferSelect, SetMem);
  and and_6 (and_6_out, BufferSelect, SetMem);
  and and_7 (and_7_out, BufferSelect, SetMem);
  and and_8 (and_8_out, BufferSelect, SetMem);
  and and_9 (and_9_out, BufferSelect, SetMem);
  and and_10 (and_10_out, BufferSelect, SetMem);
  and and_11 (and_11_out, BufferSelect, SetMem);
  and and_12 (and_12_out, BufferSelect, SetMem);
  and and_13 (and_13_out, BufferSelect, SetMem);
  and and_14 (and_14_out, BufferSelect, SetMem);
  and and_15 (and_15_out, BufferSelect, SetMem);
  and and_16 (and_16_out, BufferSelect, SetMem);
  RegSelect regselect_1 (
    .Enable(and_1_out), .Addr(adder_1_out), .AddrBus(AddrBus), .DataBus(DataBus),
    .DataOut(regselect_1_dataout), .Enabled(regselect_1_enabled));
  RegSelect regselect_2 (
    .Enable(and_2_out), .Addr(adder_2_out), .AddrBus(AddrBus), .DataBus(DataBus),
    .DataOut(regselect_2_dataout), .Enabled(regselect_2_enabled));
  RegSelect regselect_3 (
    .Enable(and_3_out), .Addr(adder_3_out), .AddrBus(AddrBus), .DataBus(DataBus),
    .DataOut(regselect_3_dataout), .Enabled(regselect_3_enabled));
  RegSelect regselect_4 (
    .Enable(and_4_out), .Addr(adder_4_out), .AddrBus(AddrBus), .DataBus(DataBus),
    .DataOut(regselect_4_dataout), .Enabled(regselect_4_enabled));
  RegSelect regselect_5 (
    .Enable(and_5_out), .Addr(adder_5_out), .AddrBus(AddrBus), .DataBus(DataBus),
    .DataOut(regselect_5_dataout), .Enabled(regselect_5_enabled));
  RegSelect regselect_6 (
    .Enable(and_6_out), .Addr(adder_6_out), .AddrBus(AddrBus), .DataBus(DataBus),
    .DataOut(regselect_6_dataout), .Enabled(regselect_6_enabled));
  RegSelect regselect_7 (
    .Enable(and_7_out), .Addr(adder_7_out), .AddrBus(AddrBus), .DataBus(DataBus),
    .DataOut(regselect_7_dataout), .Enabled(regselect_7_enabled));
  RegSelect regselect_8 (
    .Enable(and_8_out), .Addr(adder_8_out), .AddrBus(AddrBus), .DataBus(DataBus),
    .DataOut(regselect_8_dataout), .Enabled(regselect_8_enabled));
  RegSelect regselect_9 (
    .Enable(and_9_out), .Addr(adder_9_out), .AddrBus(AddrBus), .DataBus(DataBus),
    .DataOut(regselect_9_dataout), .Enabled(regselect_9_enabled));
  RegSelect regselect_10 (
    .Enable(and_10_out), .Addr(adder_10_out), .AddrBus(AddrBus), .DataBus(DataBus),
    .DataOut(regselect_10_dataout), .Enabled(regselect_10_enabled));
  RegSelect regselect_11 (
    .Enable(and_11_out), .Addr(adder_11_out), .AddrBus(AddrBus), .DataBus(DataBus),
    .DataOut(regselect_11_dataout), .Enabled(regselect_11_enabled));
  RegSelect regselect_12 (
    .Enable(and_12_out), .Addr(adder_12_out), .AddrBus(AddrBus), .DataBus(DataBus),
    .DataOut(regselect_12_dataout), .Enabled(regselect_12_enabled));
  RegSelect regselect_13 (
    .Enable(and_13_out), .Addr(adder_13_out), .AddrBus(AddrBus), .DataBus(DataBus),
    .DataOut(regselect_13_dataout), .Enabled(regselect_13_enabled));
  RegSelect regselect_14 (
    .Enable(and_14_out), .Addr(adder_14_out), .AddrBus(AddrBus), .DataBus(DataBus),
    .DataOut(regselect_14_dataout), .Enabled(regselect_14_enabled));
  RegSelect regselect_15 (
    .Enable(and_15_out), .Addr(adder_15_out), .AddrBus(AddrBus), .DataBus(DataBus),
    .DataOut(regselect_15_dataout), .Enabled(regselect_15_enabled));
  RegSelect regselect_16 (
    .Enable(and_16_out), .Addr(adder_16_out), .AddrBus(AddrBus), .DataBus(DataBus),
    .DataOut(regselect_16_dataout), .Enabled(regselect_16_enabled));
  Register #(.width(16)) register_1 (
    .D(regselect_1_dataout), .en(regselect_1_enabled), .clk(Clock), .Q(L0), .clr(Clear));
  Register #(.width(16)) register_2 (
    .D(regselect_2_dataout), .en(regselect_2_enabled), .clk(Clock), .Q(L1), .clr(Clear));
  Register #(.width(16)) register_3 (
    .D(regselect_3_dataout), .en(regselect_3_enabled), .clk(Clock), .Q(L2), .clr(Clear));
  Register #(.width(16)) register_4 (
    .D(regselect_4_dataout), .en(regselect_4_enabled), .clk(Clock), .Q(L3), .clr(Clear));
  Register #(.width(16)) register_5 (
    .D(regselect_5_dataout), .en(regselect_5_enabled), .clk(Clock), .Q(L4), .clr(Clear));
  Register #(.width(16)) register_6 (
    .D(regselect_6_dataout), .en(regselect_6_enabled), .clk(Clock), .Q(L5), .clr(Clear));
  Register #(.width(16)) register_7 (
    .D(regselect_7_dataout), .en(regselect_7_enabled), .clk(Clock), .Q(L6), .clr(Clear));
  Register #(.width(16)) register_8 (
    .D(regselect_8_dataout), .en(regselect_8_enabled), .clk(Clock), .Q(L7), .clr(Clear));
  Register #(.width(16)) register_9 (
    .D(regselect_9_dataout), .en(regselect_9_enabled), .clk(Clock), .Q(L8), .clr(Clear));
  Register #(.width(16)) register_10 (
    .D(regselect_10_dataout), .en(regselect_10_enabled), .clk(Clock), .Q(L9), .clr(Clear));
  Register #(.width(16)) register_11 (
    .D(regselect_11_dataout), .en(regselect_11_enabled), .clk(Clock), .Q(L10), .clr(Clear));
  Register #(.width(16)) register_12 (
    .D(regselect_12_dataout), .en(regselect_12_enabled), .clk(Clock), .Q(L11), .clr(Clear));
  Register #(.width(16)) register_13 (
    .D(regselect_13_dataout), .en(regselect_13_enabled), .clk(Clock), .Q(L12), .clr(Clear));
  Register #(.width(16)) register_14 (
    .D(regselect_14_dataout), .en(regselect_14_enabled), .clk(Clock), .Q(L13), .clr(Clear));
  Register #(.width(16)) register_15 (
    .D(regselect_15_dataout), .en(regselect_15_enabled), .clk(Clock), .Q(L14), .clr(Clear));
  Register #(.width(16)) register_16 (
    .D(regselect_16_dataout), .en(regselect_16_enabled), .clk(Clock), .Q(L15), .clr(Clear));
  RegSelect regselect_17 (
    .Enable(SetMem), .Addr(BaseAddr), .AddrBus(AddrBus), .DataBus(DataBus), .DataOut(regselect_17_dataout),
    .Enabled(regselect_17_enabled));
  Register #(.width(1)) register_17 (
    .D(regselect_17_dataout[0]), .en(regselect_17_enabled), .clk(Clock), .Q(BufferSelect), .clr(Clear));
  not not_1 (not_1_out, BufferSelect);
  and and_17 (and_17_out, not_1_out, SetMem);
  and and_18 (and_18_out, not_1_out, SetMem);
  and and_19 (and_19_out, not_1_out, SetMem);
  and and_20 (and_20_out, not_1_out, SetMem);
  and and_21 (and_21_out, not_1_out, SetMem);
  and and_22 (and_22_out, not_1_out, SetMem);
  and and_23 (and_23_out, not_1_out, SetMem);
  and and_24 (and_24_out, not_1_out, SetMem);
  and and_25 (and_25_out, not_1_out, SetMem);
  and and_26 (and_26_out, not_1_out, SetMem);
  and and_27 (and_27_out, not_1_out, SetMem);
  and and_28 (and_28_out, not_1_out, SetMem);
  and and_29 (and_29_out, not_1_out, SetMem);
  and and_30 (and_30_out, not_1_out, SetMem);
  and and_31 (and_31_out, not_1_out, SetMem);
  and and_32 (and_32_out, not_1_out, SetMem);
  Register #(.width(16)) register_18 (
    .D(regselect_18_dataout), .en(regselect_18_enabled), .clk(Clock), .Q(M0), .clr(Clear));
  RegSelect regselect_18 (
    .Enable(and_17_out), .Addr(adder_1_out), .AddrBus(AddrBus), .DataBus(DataBus),
    .DataOut(regselect_18_dataout), .Enabled(regselect_18_enabled));
  Register #(.width(16)) register_19 (
    .D(regselect_19_dataout), .en(regselect_19_enabled), .clk(Clock), .Q(M1), .clr(Clear));
  RegSelect regselect_19 (
    .Enable(and_18_out), .Addr(adder_2_out), .AddrBus(AddrBus), .DataBus(DataBus),
    .DataOut(regselect_19_dataout), .Enabled(regselect_19_enabled));
  Register #(.width(16)) register_20 (
    .D(regselect_20_dataout), .en(regselect_20_enabled), .clk(Clock), .Q(M2), .clr(Clear));
  RegSelect regselect_20 (
    .Enable(and_19_out), .Addr(adder_3_out), .AddrBus(AddrBus), .DataBus(DataBus),
    .DataOut(regselect_20_dataout), .Enabled(regselect_20_enabled));
  Register #(.width(16)) register_21 (
    .D(regselect_21_dataout), .en(regselect_21_enabled), .clk(Clock), .Q(M3), .clr(Clear));
  RegSelect regselect_21 (
    .Enable(and_20_out), .Addr(adder_4_out), .AddrBus(AddrBus), .DataBus(DataBus),
    .DataOut(regselect_21_dataout), .Enabled(regselect_21_enabled));
  Register #(.width(16)) register_22 (
    .D(regselect_22_dataout), .en(regselect_22_enabled), .clk(Clock), .Q(M4), .clr(Clear));
  RegSelect regselect_22 (
    .Enable(and_21_out), .Addr(adder_5_out), .AddrBus(AddrBus), .DataBus(DataBus),
    .DataOut(regselect_22_dataout), .Enabled(regselect_22_enabled));
  Register #(.width(16)) register_23 (
    .D(regselect_23_dataout), .en(regselect_23_enabled), .clk(Clock), .Q(M5), .clr(Clear));
  RegSelect regselect_23 (
    .Enable(and_22_out), .Addr(adder_6_out), .AddrBus(AddrBus), .DataBus(DataBus),
    .DataOut(regselect_23_dataout), .Enabled(regselect_23_enabled));
  Register #(.width(16)) register_24 (
    .D(regselect_24_dataout), .en(regselect_24_enabled), .clk(Clock), .Q(M6), .clr(Clear));
  RegSelect regselect_24 (
    .Enable(and_23_out), .Addr(adder_7_out), .AddrBus(AddrBus), .DataBus(DataBus),
    .DataOut(regselect_24_dataout), .Enabled(regselect_24_enabled));
  Register #(.width(16)) register_25 (
    .D(regselect_25_dataout), .en(regselect_25_enabled), .clk(Clock), .Q(M7), .clr(Clear));
  RegSelect regselect_25 (
    .Enable(and_24_out), .Addr(adder_8_out), .AddrBus(AddrBus), .DataBus(DataBus),
    .DataOut(regselect_25_dataout), .Enabled(regselect_25_enabled));
  Register #(.width(16)) register_26 (
    .D(regselect_26_dataout), .en(regselect_26_enabled), .clk(Clock), .Q(M8), .clr(Clear));
  RegSelect regselect_26 (
    .Enable(and_25_out), .Addr(adder_9_out), .AddrBus(AddrBus), .DataBus(DataBus),
    .DataOut(regselect_26_dataout), .Enabled(regselect_26_enabled));
  Register #(.width(16)) register_27 (
    .D(regselect_27_dataout), .en(regselect_27_enabled), .clk(Clock), .Q(M9), .clr(Clear));
  RegSelect regselect_27 (
    .Enable(and_26_out), .Addr(adder_10_out), .AddrBus(AddrBus), .DataBus(DataBus),
    .DataOut(regselect_27_dataout), .Enabled(regselect_27_enabled));
  Register #(.width(16)) register_28 (
    .D(regselect_28_dataout), .en(regselect_28_enabled), .clk(Clock), .Q(M10), .clr(Clear));
  RegSelect regselect_28 (
    .Enable(and_27_out), .Addr(adder_11_out), .AddrBus(AddrBus), .DataBus(DataBus),
    .DataOut(regselect_28_dataout), .Enabled(regselect_28_enabled));
  Register #(.width(16)) register_29 (
    .D(regselect_29_dataout), .en(regselect_29_enabled), .clk(Clock), .Q(M11), .clr(Clear));
  RegSelect regselect_29 (
    .Enable(and_28_out), .Addr(adder_12_out), .AddrBus(AddrBus), .DataBus(DataBus),
    .DataOut(regselect_29_dataout), .Enabled(regselect_29_enabled));
  Register #(.width(16)) register_30 (
    .D(regselect_30_dataout), .en(regselect_30_enabled), .clk(Clock), .Q(M12), .clr(Clear));
  RegSelect regselect_30 (
    .Enable(and_29_out), .Addr(adder_13_out), .AddrBus(AddrBus), .DataBus(DataBus),
    .DataOut(regselect_30_dataout), .Enabled(regselect_30_enabled));
  Register #(.width(16)) register_31 (
    .D(regselect_31_dataout), .en(regselect_31_enabled), .clk(Clock), .Q(M13), .clr(Clear));
  RegSelect regselect_31 (
    .Enable(and_30_out), .Addr(adder_14_out), .AddrBus(AddrBus), .DataBus(DataBus),
    .DataOut(regselect_31_dataout), .Enabled(regselect_31_enabled));
  Register #(.width(16)) register_32 (
    .D(regselect_32_dataout), .en(regselect_32_enabled), .clk(Clock), .Q(M14), .clr(Clear));
  RegSelect regselect_32 (
    .Enable(and_31_out), .Addr(adder_15_out), .AddrBus(AddrBus), .DataBus(DataBus),
    .DataOut(regselect_32_dataout), .Enabled(regselect_32_enabled));
  Register #(.width(16)) register_33 (
    .D(regselect_33_dataout), .en(regselect_33_enabled), .clk(Clock), .Q(M15), .clr(Clear));
  RegSelect regselect_33 (
    .Enable(and_32_out), .Addr(adder_16_out), .AddrBus(AddrBus), .DataBus(DataBus),
    .DataOut(regselect_33_dataout), .Enabled(regselect_33_enabled));
  Multiplexer #(.width(16)) multiplexer_1 (.in0(L0), .in1(M0), .out(R0), .sel(BufferSelect));
  Multiplexer #(.width(16)) multiplexer_2 (.in0(L1), .in1(M1), .out(R1), .sel(BufferSelect));
  Multiplexer #(.width(16)) multiplexer_3 (.in0(L2), .in1(M2), .out(R2), .sel(BufferSelect));
  Multiplexer #(.width(16)) multiplexer_4 (.in0(L3), .in1(M3), .out(R3), .sel(BufferSelect));
  Multiplexer #(.width(16)) multiplexer_5 (.in0(L4), .in1(M4), .out(R4), .sel(BufferSelect));
  Multiplexer #(.width(16)) multiplexer_6 (.in0(L5), .in1(M5), .out(R5), .sel(BufferSelect));
  Multiplexer #(.width(16)) multiplexer_7 (.in0(L6), .in1(M6), .out(R6), .sel(BufferSelect));
  Multiplexer #(.width(16)) multiplexer_8 (.in0(L7), .in1(M7), .out(R7), .sel(BufferSelect));
  Multiplexer #(.width(16)) multiplexer_9 (.in0(L8), .in1(M8), .out(R8), .sel(BufferSelect));
  Multiplexer #(.width(16)) multiplexer_10 (.in0(L9), .in1(M9), .out(R9), .sel(BufferSelect));
  Multiplexer #(.width(16)) multiplexer_11 (.in0(L10), .in1(M10), .out(R10), .sel(BufferSelect));
  Multiplexer #(.width(16)) multiplexer_12 (.in0(L11), .in1(M11), .out(R11), .sel(BufferSelect));
  Multiplexer #(.width(16)) multiplexer_13 (.in0(L12), .in1(M12), .out(R12), .sel(BufferSelect));
  Multiplexer #(.width(16)) multiplexer_14 (.in0(L13), .in1(M13), .out(R13), .sel(BufferSelect));
  Multiplexer #(.width(16)) multiplexer_15 (.in0(L14), .in1(M14), .out(R14), .sel(BufferSelect));
  Multiplexer #(.width(16)) multiplexer_16 (.in0(L15), .in1(M15), .out(R15), .sel(BufferSelect));
endmodule

module UAL_circ (
  input  [3:0] Code_UAL,
  input  [15:0] A,
  input  [15:0] B,
  output Z,
  output V,
  output [15:0] S,
  output C
);

  wire C0, C1, C2, C3, comparator_1_eq, demultiplexer_1_out0, demultiplexer_1_out1, demultiplexer_1_out2,
       demultiplexer_1_out3, demultiplexer_1_out4, demultiplexer_1_out5, demultiplexer_1_out11;
  wire [15:0] adder_1_out, adder_2_out, and_1_out, C4, multiplier_1_out, not_1_out, not_2_out, or_1_out,
       shifter_1_out, subtractor_1_out, subtractor_2_out;

  assign and_1_out = A & B;  // AND_Gate and_1, 16 bits wide
  assign or_1_out = A | B;  // OR_Gate or_1, 16 bits wide
  assign not_1_out = ~A;  // NOT_Gate not_1, 16 bits wide
  assign not_2_out = ~B;  // NOT_Gate not_2, 16 bits wide
  Adder #(.width(16)) adder_1 (.a(A), .b(B), .out(adder_1_out), .cout(C0));  // open: cin
  Subtractor #(.width(16)) subtractor_1 (.a(A), .b(B), .out(subtractor_1_out), .bout(C1));  // open: bin
  Adder #(.width(16)) adder_2 (.a(A), .b({16{1'b0}}), .out(adder_2_out), .cin(1'b1), .cout(C2));
  Subtractor #(.width(16)) subtractor_2 (.a(A), .b(16'h1), .out(subtractor_2_out), .bout(C3));  // open: bin
  Multiplier #(.width(16)) multiplier_1 (.a(A), .b(B), .out(multiplier_1_out), .cout(C4));  // open: cin
  Shifter #(.shift("lr"), .width(16)) shifter_1 (.in(A), .\dist (4'b0001), .out(shifter_1_out));
  Multiplexer #(.select(4), .width(16)) multiplexer_1 (
    .in0(A), .in1(B), .in2(and_1_out), .in3(or_1_out), .in4(not_1_out), .in5(not_2_out), .in6(adder_1_out),
    .in7(subtractor_1_out), .in8(adder_2_out), .in9(subtractor_2_out), .in10(multiplier_1_out),
    .in11(shifter_1_out), .out(S), .sel(Code_UAL));  // open: in12, in13, in14, in15
  Comparator #(.width(16)) comparator_1 (.a(C4), .b({16{1'b0}}), .eq(comparator_1_eq));  // open: gt, lt
  Comparator #(.mode("unsigned"), .width(16)) comparator_2 (.a({16{1'b0}}), .b(S), .eq(Z));  // open: gt, lt
  Demultiplexer #(.select(4)) demultiplexer_1 (
    .out0(demultiplexer_1_out0), .out1(demultiplexer_1_out1), .out2(demultiplexer_1_out2),
    .out3(demultiplexer_1_out3), .out4(demultiplexer_1_out4), .out5(demultiplexer_1_out5), .out6(C0),
    .out7(C1), .out8(C2), .out9(C3), .out10(comparator_1_eq), .out11(demultiplexer_1_out11), .in(C));  // open: out12, out13, out14, out15, sel
  // also tied to GND on the sheet: {demultiplexer_1_out0, demultiplexer_1_out1, demultiplexer_1_out2, demultiplexer_1_out3, demultiplexer_1_out4, demultiplexer_1_out5, demultiplexer_1_out11}
endmodule
