// Logisim project archi_jeu.circ as structural Verilog: 4 circuits, main circuit main
module main (
);

  wire and_1_out, and_2_out, and_3_out, and_4_out, and_5_out, and_6_out, Clear, ClearIF, clk,
       comparator_1_eq, comparator_2_eq, comparator_3_eq, IFlag, INTA, INTR, not_1_out, or_1_out, ReadA,
       ReadB, ReadINTAddr, ReadMem, ReadPC, ReadSP, SetA, SetB, SetIF, SetMem, SetPC, SetRADM, SetSP, Z;
  wire [1:0] MuxSel_smux;
  wire [2:0] CodeMCount;
  wire [3:0] BinaryToBCD_1_d0, BinaryToBCD_1_d1, BinaryToBCD_1_d2, BinaryToBCD_1_d3, BinaryToBCD_1_d4,
       BinaryToBCD_2_d0, BinaryToBCD_2_d1, BinaryToBCD_2_d2, BinaryToBCD_2_d3, BinaryToBCD_2_d4,
       BinaryToBCD_3_d0, BinaryToBCD_3_d1, BinaryToBCD_3_d2, BinaryToBCD_3_d3, BinaryToBCD_3_d4, Code_UAL;
  wire [7:0] adder_1_out, JMP_Adr, MicroPC_q, multiplexer_1_out, pull_resistor_2_node, pull_resistor_2_node_2;
  wire [15:0] A_q, AddrBus, B_q, controlled_buffer_1_out, controlled_buffer_4_out, controlled_buffer_5_out,
       controlled_buffer_8_out, controlled_buffer_10_out, controlled_buffer_12_out, controlled_buffer_13_out,
       controlled_buffer_15_out, controlled_buffer_17_out, DBus, MainMemory_dout, PC_q, pull_resistor_1_node,
       register_1_q, register_2_q, register_4_q, SP_q, UAL_1_s;
  wire [31:30] Sequencer_data;

  Button Reset (.out(Clear));
  Clock clock_1 (.out(clk));
  not not_1 (not_1_out, AddrBus[12]);
  LED MemSelected (.in(not_1_out));
  assign controlled_buffer_1_out = SetMem ? DBus : 16'bz;  // Controlled_Buffer controlled_buffer_1
  and and_1 (and_1_out, SetMem, not_1_out);
  and and_2 (and_2_out, ReadMem, not_1_out);
  RAM #(.addrWidth(16), .dataWidth(16), .trigger("falling")) MainMemory (
    .addr(AddrBus), .we(and_1_out), .oe(and_2_out), .clk(clk), .din(controlled_buffer_1_out),
    .dout(MainMemory_dout));
  and and_3 (and_3_out, SetMem, comparator_1_eq);
  Comparator #(.mode("unsigned"), .width(16)) comparator_1 (
    .a(AddrBus), .b(16'h1000), .eq(comparator_1_eq));  // open: gt, lt
  Pull_Resistor pull_resistor_1 (.node(pull_resistor_1_node));
  Pull_Resistor pull_resistor_2 (.node({pull_resistor_2_node_2, pull_resistor_2_node}));
  assign {pull_resistor_2_node_2, pull_resistor_2_node} = ReadMem ? DBus : 16'bz;  // Controlled_Buffer controlled_buffer_2
  assign DBus = SetMem ? UAL_1_s : 16'bz;  // Controlled_Buffer controlled_buffer_3
  assign controlled_buffer_4_out = and_3_out ? DBus : 16'bz;  // Controlled_Buffer controlled_buffer_4
  assign controlled_buffer_5_out = SetRADM ? UAL_1_s : 16'bz;  // Controlled_Buffer controlled_buffer_5
  Register #(.width(16)) register_1 (
    .D(controlled_buffer_4_out), .en(and_3_out), .clk(clk), .Q(register_1_q), .clr(Clear));
  assign DBus = ReadMem ? MainMemory_dout : 16'bz;  // Controlled_Buffer controlled_buffer_6
  Register #(.width(16)) Radm (.D(controlled_buffer_5_out), .en(SetRADM), .clk(clk), .Q(AddrBus), .clr(Clear));
  assign pull_resistor_1_node = ReadINTAddr ? 16'h2 : 16'bz;  // Controlled_Buffer controlled_buffer_7
  assign controlled_buffer_8_out = SetA ? UAL_1_s : 16'bz;  // Controlled_Buffer controlled_buffer_8
  Hex_Digit_Display Hex_Digit_Display_1 (.value(BinaryToBCD_1_d4));  // open: dp
  Hex_Digit_Display Hex_Digit_Display_2 (.value(BinaryToBCD_1_d3));  // open: dp
  BinaryToBCD BinaryToBCD_1 (
    .Input_bus_1(register_1_q), .D4(BinaryToBCD_1_d4), .D3(BinaryToBCD_1_d3), .D2(BinaryToBCD_1_d2),
    .D1(BinaryToBCD_1_d1), .D0(BinaryToBCD_1_d0));
  Register #(.width(16)) A (.D(controlled_buffer_8_out), .en(SetA), .clk(clk), .Q(A_q), .clr(Clear));
  Hex_Digit_Display Hex_Digit_Display_4 (.value(BinaryToBCD_1_d1));  // open: dp
  Hex_Digit_Display Hex_Digit_Display_3 (.value(BinaryToBCD_1_d2));  // open: dp
  assign pull_resistor_1_node = ReadA ? A_q : 16'bz;  // Controlled_Buffer controlled_buffer_9
  Hex_Digit_Display Hex_Digit_Display_5 (.value(BinaryToBCD_1_d0));  // open: dp
  Adder adder_1 (.a(MicroPC_q), .b(8'h1), .out(adder_1_out));  // open: cin, cout
  Register #(.width(16)) B (.D(controlled_buffer_10_out), .en(SetB), .clk(clk), .Q(B_q), .clr(Clear));
  assign controlled_buffer_10_out = SetB ? UAL_1_s : 16'bz;  // Controlled_Buffer controlled_buffer_10
  Multiplexer #(.select(2), .width(8)) multiplexer_1 (
    .in0(adder_1_out), .in1(JMP_Adr), .in2(pull_resistor_2_node_2), .out(multiplexer_1_out), .sel(MuxSel_smux));  // open: in3
  MuxSelOpt MuxSel (.CodeMCount(CodeMCount), .Z(Z), .INTR_IF(and_4_out), .SMux(MuxSel_smux));
  and and_4 (and_4_out, IFlag, INTR);
  assign {pull_resistor_2_node_2, pull_resistor_2_node} = ReadB ? B_q : 16'bz;  // Controlled_Buffer controlled_buffer_11
  and and_5 (and_5_out, SetMem, comparator_2_eq);
  Comparator #(.mode("unsigned"), .width(16)) comparator_2 (
    .a(AddrBus), .b(16'h1001), .eq(comparator_2_eq));  // open: gt, lt
  Register #(.width(16)) PC (.D(controlled_buffer_12_out), .en(SetPC), .clk(clk), .Q(PC_q), .clr(Clear));
  assign controlled_buffer_12_out = SetPC ? UAL_1_s : 16'bz;  // Controlled_Buffer controlled_buffer_12
  assign controlled_buffer_13_out = and_5_out ? DBus : 16'bz;  // Controlled_Buffer controlled_buffer_13
  Register MicroPC (.D(multiplexer_1_out), .en(1'b1), .clk(clk), .Q(MicroPC_q), .clr(Clear));
  assign pull_resistor_1_node = ReadPC ? PC_q : 16'bz;  // Controlled_Buffer controlled_buffer_14
  Register #(.width(16)) register_2 (
    .D(controlled_buffer_13_out), .en(and_5_out), .clk(clk), .Q(register_2_q), .clr(Clear));
  assign controlled_buffer_15_out = SetSP ? UAL_1_s : 16'bz;  // Controlled_Buffer controlled_buffer_15
  Register #(.width(16)) SP (.D(controlled_buffer_15_out), .en(SetSP), .clk(clk), .Q(SP_q), .clr(Clear));
  assign pull_resistor_1_node = ReadSP ? SP_q : 16'bz;  // Controlled_Buffer controlled_buffer_16
  Hex_Digit_Display Hex_Digit_Display_6 (.value(BinaryToBCD_2_d4));  // open: dp
  Hex_Digit_Display Hex_Digit_Display_7 (.value(BinaryToBCD_2_d3));  // open: dp
  BinaryToBCD BinaryToBCD_2 (
    .Input_bus_1(register_2_q), .D4(BinaryToBCD_2_d4), .D3(BinaryToBCD_2_d3), .D2(BinaryToBCD_2_d2),
    .D1(BinaryToBCD_2_d1), .D0(BinaryToBCD_2_d0));
  ROM #(.dataWidth(32)) Sequencer (
    .addr(MicroPC_q),
    .data({Sequencer_data, ReadINTAddr, ClearIF, SetIF, INTA, CodeMCount, Code_UAL, SetSP, ReadSP, SetB, ReadB, SetA, ReadA, SetPC, ReadPC, SetRADM, SetMem, ReadMem, JMP_Adr}));
  Hex_Digit_Display Hex_Digit_Display_8 (.value(BinaryToBCD_2_d2));  // open: dp
  Hex_Digit_Display Hex_Digit_Display_9 (.value(BinaryToBCD_2_d1));  // open: dp
  Hex_Digit_Display Hex_Digit_Display_10 (.value(BinaryToBCD_2_d0));  // open: dp
  or or_1 (or_1_out, ClearIF, SetIF);
  Register #(.width(1)) register_3 (.D(SetIF), .en(or_1_out), .clk(clk), .Q(IFlag), .clr(Clear));
  and and_6 (and_6_out, SetMem, comparator_3_eq);
  Comparator #(.mode("unsigned"), .width(16)) comparator_3 (
    .a(AddrBus), .b(16'h1002), .eq(comparator_3_eq));  // open: gt, lt
  assign controlled_buffer_17_out = and_6_out ? DBus : 16'bz;  // Controlled_Buffer controlled_buffer_17
  Register #(.width(16)) register_4 (
    .D(controlled_buffer_17_out), .en(and_6_out), .clk(clk), .Q(register_4_q), .clr(Clear));
  Hex_Digit_Display Hex_Digit_Display_11 (.value(BinaryToBCD_3_d4));  // open: dp
  Hex_Digit_Display Hex_Digit_Display_12 (.value(BinaryToBCD_3_d3));  // open: dp
  BinaryToBCD BinaryToBCD_3 (
    .Input_bus_1(register_4_q), .D4(BinaryToBCD_3_d4), .D3(BinaryToBCD_3_d3), .D2(BinaryToBCD_3_d2),
    .D1(BinaryToBCD_3_d1), .D0(BinaryToBCD_3_d0));
  UAL UAL_1 (
    .Code_UAL(Code_UAL), .A(pull_resistor_1_node), .B({pull_resistor_2_node_2, pull_resistor_2_node}), .Z(Z),
    .S(UAL_1_s));  // open: V, C
  Hex_Digit_Display Hex_Digit_Display_13 (.value(BinaryToBCD_3_d2));  // open: dp
  Hex_Digit_Display Hex_Digit_Display_14 (.value(BinaryToBCD_3_d1));  // open: dp
  Hex_Digit_Display Hex_Digit_Display_15 (.value(BinaryToBCD_3_d0));  // open: dp

  // Notes on the sheet:
  //   Is the memory selected ?
  //   Bus B
  //   Bus A
  //   contents of Sequencer (hex, n*v repeats v):
  //   800008 7*0 c00 1401900 0 0 80000c 0 0 0 c00 84100 c01800 0 c00 80500 84100 c01800 4*0 c00 80500 2200
  //   c01800 c00 90100 c01800 0 c00 80500 90100 c01800 4*0 c00 80500 8a200 c01800 b0e000 0 0 0 b1a000 0 0
  //   0 b8e000 0 0 0 b9a000 0 0 0 d0e000 0 0 0 d1a000 0 0 0 d86000 7*0 90e000 0 0 0 91a000 0 0 0 98e000 0
  //   0 0 99a000 0 0 0 a06000 0 0 0 a98000 11*0 c00 881100 0 0 1802076 c01800 c00 881100 188807a c01800
  //   c00 881100 4*0 c00 c0100 c01800 0 c00 80500 c0100 c01800 4*0 c00 80500 20200 c01800 c60000 0 0 0
  //   ce0000 11*0 20400 400a00 4e0000 c00 881100 0 0 0 460400 881100 6*0 20400 2200 ce0000 0 460400 884100
  //   0 0 c00 320500 2200 c01800 c00 320500 84100 c01800 20400 88200 ce0000 0 460400 890100 0 0 c00 320500
  //   88200 c01800 c00 320500 90100 c01800
endmodule

module MuxSelOpt (
  input  [2:0] CodeMCount,
  input  Z,
  input  INTR_IF,
  output [1:0] SMux
);

  wire and_2_out, and_3_out, and_4_out, not_1_out, not_2_out, not_3_out;

  not not_1 (not_1_out, CodeMCount[1]);
  not not_2 (not_2_out, CodeMCount[0]);
  not not_3 (not_3_out, INTR_IF);
  and and_1 (SMux[1], CodeMCount[1], not_2_out);
  and and_2 (and_2_out, not_1_out, CodeMCount[0]);
  and and_3 (and_3_out, CodeMCount[0], Z);
  and and_4 (and_4_out, CodeMCount[2], not_3_out);
  or or_1 (SMux[0], and_2_out, and_3_out, and_4_out);
endmodule

module Add3 (
  input  A3,
  input  A2,
  input  A1,
  input  A0,
  output S3,
  output S2,
  output S1,
  output S0
);

  wire and_1_out, and_2_out, and_3_out, and_4_out, and_5_out, and_6_out, and_7_out, and_8_out, and_9_out,
       and_10_out, not_1_out, not_2_out, not_3_out, not_4_out;

  not not_1 (not_1_out, A3);
  not not_2 (not_2_out, A2);
  not not_3 (not_3_out, A1);
  not not_4 (not_4_out, A0);
  and and_1 (and_1_out, A2, A0);
  and and_2 (and_2_out, A2, A1);
  and and_3 (and_3_out, A2, not_3_out, not_4_out);
  and and_4 (and_4_out, A3, A0);
  and and_5 (and_5_out, not_2_out, A1);
  and and_6 (and_6_out, A1, A0);
  and and_7 (and_7_out, A3, not_4_out);
  and and_8 (and_8_out, not_1_out, not_2_out, A0);
  and and_9 (and_9_out, A2, A1, not_4_out);
  and and_10 (and_10_out, A3, not_4_out);
  or or_1 (S3, and_1_out, and_2_out, A3);
  or or_2 (S2, and_3_out, and_4_out);
  or or_3 (S1, and_5_out, and_6_out, and_7_out);
  or or_4 (S0, and_8_out, and_9_out, and_10_out);
endmodule

module BinaryToBCD (
  input  [15:0] Input_bus_1,
  output [3:0] D4,
  output [3:0] D3,
  output [3:0] D2,
  output [3:0] D1,
  output [3:0] D0
);

  wire Add3_1_s0, Add3_1_s1, Add3_1_s2, Add3_1_s3, Add3_2_s0, Add3_2_s1, Add3_2_s2, Add3_2_s3, Add3_3_s0,
       Add3_3_s1, Add3_3_s2, Add3_3_s3, Add3_4_s0, Add3_4_s1, Add3_4_s2, Add3_4_s3, Add3_5_s0, Add3_5_s1,
       Add3_5_s2, Add3_5_s3, Add3_6_s0, Add3_6_s1, Add3_6_s2, Add3_6_s3, Add3_7_s0, Add3_7_s1, Add3_7_s2,
       Add3_7_s3, Add3_8_s0, Add3_8_s1, Add3_8_s2, Add3_8_s3, Add3_9_s0, Add3_9_s1, Add3_9_s2, Add3_9_s3,
       Add3_10_s0, Add3_10_s1, Add3_10_s2, Add3_10_s3, Add3_11_s0, Add3_11_s1, Add3_11_s2, Add3_11_s3,
       Add3_12_s0, Add3_12_s1, Add3_12_s2, Add3_12_s3, Add3_13_s0, Add3_13_s1, Add3_13_s2, Add3_13_s3,
       Add3_14_s0, Add3_14_s1, Add3_14_s2, Add3_14_s3, Add3_15_s0, Add3_15_s1, Add3_15_s2, Add3_15_s3,
       Add3_16_s0, Add3_16_s1, Add3_16_s2, Add3_16_s3, Add3_17_s0, Add3_17_s1, Add3_17_s2, Add3_17_s3,
       Add3_18_s0, Add3_18_s1, Add3_18_s2, Add3_18_s3, Add3_19_s0, Add3_19_s1, Add3_19_s2, Add3_19_s3,
       Add3_20_s0, Add3_20_s1, Add3_20_s2, Add3_20_s3, Add3_21_s0, Add3_21_s1, Add3_21_s2, Add3_21_s3,
       Add3_22_s0, Add3_22_s1, Add3_22_s2, Add3_22_s3, Add3_23_s0, Add3_23_s1, Add3_23_s2, Add3_23_s3,
       Add3_24_s0, Add3_24_s1, Add3_24_s2, Add3_24_s3, Add3_25_s0, Add3_25_s1, Add3_25_s2, Add3_25_s3,
       Add3_26_s0, Add3_26_s1, Add3_26_s2, Add3_26_s3, Add3_27_s0, Add3_27_s1, Add3_27_s2, Add3_27_s3,
       Add3_28_s0, Add3_28_s1, Add3_28_s2, Add3_28_s3, Add3_29_s0, Add3_29_s1, Add3_29_s2, Add3_29_s3,
       Add3_30_s0, Add3_30_s1, Add3_30_s2, Add3_30_s3;

  Add3 Add3_31 (
    .A0(Add3_27_s3), .A3(1'b0), .A2(Add3_19_s3), .A1(Add3_23_s3), .S2(D4[3]), .S1(D4[2]), .S0(D4[1]));  // open: S3
  Add3 Add3_1 (
    .A0(Input_bus_1[13]), .A3(1'b0), .A2(Input_bus_1[15]), .A1(Input_bus_1[14]), .S3(Add3_1_s3),
    .S2(Add3_1_s2), .S1(Add3_1_s1), .S0(Add3_1_s0));
  Add3 Add3_4 (
    .A0(Add3_3_s3), .A3(1'b0), .A2(Add3_1_s3), .A1(Add3_2_s3), .S3(Add3_4_s3), .S2(Add3_4_s2),
    .S1(Add3_4_s1), .S0(Add3_4_s0));
  Add3 Add3_6 (
    .A0(Add3_5_s3), .A3(Add3_4_s2), .A2(Add3_4_s1), .A1(Add3_4_s0), .S3(Add3_6_s3), .S2(Add3_6_s2),
    .S1(Add3_6_s1), .S0(Add3_6_s0));
  Add3 Add3_10 (
    .A0(Add3_8_s3), .A3(1'b0), .A2(Add3_4_s3), .A1(Add3_6_s3), .S3(Add3_10_s3), .S2(Add3_10_s2),
    .S1(Add3_10_s1), .S0(Add3_10_s0));
  Add3 Add3_13 (
    .A0(Add3_11_s3), .A3(Add3_10_s2), .A2(Add3_10_s1), .A1(Add3_10_s0), .S3(Add3_13_s3), .S2(Add3_13_s2),
    .S1(Add3_13_s1), .S0(Add3_13_s0));
  Add3 Add3_16 (
    .A0(Add3_14_s3), .A3(Add3_13_s2), .A2(Add3_13_s1), .A1(Add3_13_s0), .S3(Add3_16_s3), .S2(Add3_16_s2),
    .S1(Add3_16_s1), .S0(Add3_16_s0));
  Add3 Add3_19 (
    .A0(Add3_16_s3), .A3(1'b0), .A2(Add3_10_s3), .A1(Add3_13_s3), .S3(Add3_19_s3), .S2(Add3_19_s2),
    .S1(Add3_19_s1), .S0(Add3_19_s0));
  Add3 Add3_23 (
    .A0(Add3_20_s3), .A3(Add3_19_s2), .A2(Add3_19_s1), .A1(Add3_19_s0), .S3(Add3_23_s3), .S2(Add3_23_s2),
    .S1(Add3_23_s1), .S0(Add3_23_s0));
  Add3 Add3_27 (
    .A0(Add3_24_s3), .A3(Add3_23_s2), .A2(Add3_23_s1), .A1(Add3_23_s0), .S3(Add3_27_s3), .S2(Add3_27_s2),
    .S1(Add3_27_s1), .S0(Add3_27_s0));
  Add3 Add3_32 (
    .A0(Add3_28_s3), .A3(Add3_27_s2), .A2(Add3_27_s1), .A1(Add3_27_s0), .S3(D4[0]), .S2(D3[3]), .S1(D3[2]),
    .S0(D3[1]));
  Add3 Add3_2 (
    .A0(Input_bus_1[12]), .A3(Add3_1_s2), .A2(Add3_1_s1), .A1(Add3_1_s0), .S3(Add3_2_s3), .S2(Add3_2_s2),
    .S1(Add3_2_s1), .S0(Add3_2_s0));
  Add3 Add3_3 (
    .A0(Input_bus_1[11]), .A3(Add3_2_s2), .A2(Add3_2_s1), .A1(Add3_2_s0), .S3(Add3_3_s3), .S2(Add3_3_s2),
    .S1(Add3_3_s1), .S0(Add3_3_s0));
  Add3 Add3_5 (
    .A0(Input_bus_1[10]), .A3(Add3_3_s2), .A2(Add3_3_s1), .A1(Add3_3_s0), .S3(Add3_5_s3), .S2(Add3_5_s2),
    .S1(Add3_5_s1), .S0(Add3_5_s0));
  Add3 Add3_7 (
    .A0(Input_bus_1[9]), .A3(Add3_5_s2), .A2(Add3_5_s1), .A1(Add3_5_s0), .S3(Add3_7_s3), .S2(Add3_7_s2),
    .S1(Add3_7_s1), .S0(Add3_7_s0));
  Add3 Add3_8 (
    .A0(Add3_7_s3), .A3(Add3_6_s2), .A2(Add3_6_s1), .A1(Add3_6_s0), .S3(Add3_8_s3), .S2(Add3_8_s2),
    .S1(Add3_8_s1), .S0(Add3_8_s0));
  Add3 Add3_11 (
    .A0(Add3_9_s3), .A3(Add3_8_s2), .A2(Add3_8_s1), .A1(Add3_8_s0), .S3(Add3_11_s3), .S2(Add3_11_s2),
    .S1(Add3_11_s1), .S0(Add3_11_s0));
  Add3 Add3_14 (
    .A0(Add3_12_s3), .A3(Add3_11_s2), .A2(Add3_11_s1), .A1(Add3_11_s0), .S3(Add3_14_s3), .S2(Add3_14_s2),
    .S1(Add3_14_s1), .S0(Add3_14_s0));
  Add3 Add3_17 (
    .A0(Add3_15_s3), .A3(Add3_14_s2), .A2(Add3_14_s1), .A1(Add3_14_s0), .S3(Add3_17_s3), .S2(Add3_17_s2),
    .S1(Add3_17_s1), .S0(Add3_17_s0));
  Add3 Add3_20 (
    .A0(Add3_17_s3), .A3(Add3_16_s2), .A2(Add3_16_s1), .A1(Add3_16_s0), .S3(Add3_20_s3), .S2(Add3_20_s2),
    .S1(Add3_20_s1), .S0(Add3_20_s0));
  Add3 Add3_24 (
    .A0(Add3_21_s3), .A3(Add3_20_s2), .A2(Add3_20_s1), .A1(Add3_20_s0), .S3(Add3_24_s3), .S2(Add3_24_s2),
    .S1(Add3_24_s1), .S0(Add3_24_s0));
  Add3 Add3_28 (
    .A0(Add3_25_s3), .A3(Add3_24_s2), .A2(Add3_24_s1), .A1(Add3_24_s0), .S3(Add3_28_s3), .S2(Add3_28_s2),
    .S1(Add3_28_s1), .S0(Add3_28_s0));
  Add3 Add3_33 (
    .A0(Add3_29_s3), .A3(Add3_28_s2), .A2(Add3_28_s1), .A1(Add3_28_s0), .S3(D3[0]), .S2(D2[3]), .S1(D2[2]),
    .S0(D2[1]));
  Add3 Add3_9 (
    .A0(Input_bus_1[8]), .A3(Add3_7_s2), .A2(Add3_7_s1), .A1(Add3_7_s0), .S3(Add3_9_s3), .S2(Add3_9_s2),
    .S1(Add3_9_s1), .S0(Add3_9_s0));
  Add3 Add3_12 (
    .A0(Input_bus_1[7]), .A3(Add3_9_s2), .A2(Add3_9_s1), .A1(Add3_9_s0), .S3(Add3_12_s3), .S2(Add3_12_s2),
    .S1(Add3_12_s1), .S0(Add3_12_s0));
  Add3 Add3_15 (
    .A0(Input_bus_1[6]), .A3(Add3_12_s2), .A2(Add3_12_s1), .A1(Add3_12_s0), .S3(Add3_15_s3), .S2(Add3_15_s2),
    .S1(Add3_15_s1), .S0(Add3_15_s0));
  Add3 Add3_18 (
    .A0(Input_bus_1[5]), .A3(Add3_15_s2), .A2(Add3_15_s1), .A1(Add3_15_s0), .S3(Add3_18_s3), .S2(Add3_18_s2),
    .S1(Add3_18_s1), .S0(Add3_18_s0));
  Add3 Add3_21 (
    .A0(Add3_18_s3), .A3(Add3_17_s2), .A2(Add3_17_s1), .A1(Add3_17_s0), .S3(Add3_21_s3), .S2(Add3_21_s2),
    .S1(Add3_21_s1), .S0(Add3_21_s0));
  Add3 Add3_25 (
    .A0(Add3_22_s3), .A3(Add3_21_s2), .A2(Add3_21_s1), .A1(Add3_21_s0), .S3(Add3_25_s3), .S2(Add3_25_s2),
    .S1(Add3_25_s1), .S0(Add3_25_s0));
  Add3 Add3_29 (
    .A0(Add3_26_s3), .A3(Add3_25_s2), .A2(Add3_25_s1), .A1(Add3_25_s0), .S3(Add3_29_s3), .S2(Add3_29_s2),
    .S1(Add3_29_s1), .S0(Add3_29_s0));
  Add3 Add3_34 (
    .A0(Add3_30_s3), .A3(Add3_29_s2), .A2(Add3_29_s1), .A1(Add3_29_s0), .S3(D2[0]), .S2(D1[3]), .S1(D1[2]),
    .S0(D1[1]));
  Add3 Add3_22 (
    .A0(Input_bus_1[4]), .A3(Add3_18_s2), .A2(Add3_18_s1), .A1(Add3_18_s0), .S3(Add3_22_s3), .S2(Add3_22_s2),
    .S1(Add3_22_s1), .S0(Add3_22_s0));
  Add3 Add3_26 (
    .A0(Input_bus_1[3]), .A3(Add3_22_s2), .A2(Add3_22_s1), .A1(Add3_22_s0), .S3(Add3_26_s3), .S2(Add3_26_s2),
    .S1(Add3_26_s1), .S0(Add3_26_s0));
  Add3 Add3_30 (
    .A0(Input_bus_1[2]), .A3(Add3_26_s2), .A2(Add3_26_s1), .A1(Add3_26_s0), .S3(Add3_30_s3), .S2(Add3_30_s2),
    .S1(Add3_30_s1), .S0(Add3_30_s0));
  Add3 Add3_35 (
    .A0(Input_bus_1[1]), .A3(Add3_30_s2), .A2(Add3_30_s1), .A1(Add3_30_s0), .S3(D1[0]), .S2(D0[3]),
    .S1(D0[2]), .S0(D0[1]));

  assign D0[0] = Input_bus_1[0];
endmodule
