// Logisim project archi_seq_man_evolution.circ as structural Verilog: 1 circuit, main circuit main
module main (
  input  [3:0] in_1,
  input  SetB,
  input  ReadB,
  input  SetA,
  input  ReadA,
  input  SetMem,
  input  ReadMem,
  input  [15:0] Data
);

  wire Clear, clk, ual_1_p4;
  wire [15:0] A_q, B_q, controlled_buffer_2_out, controlled_buffer_4_out, pull_resistor_1_node,
       pull_resistor_2_node, ual_1_p5;

  Pull_Resistor pull_resistor_1 (.node(pull_resistor_1_node));
  assign pull_resistor_1_node = ReadMem ? Data : 16'bz;  // Controlled_Buffer controlled_buffer_1
  Pull_Resistor pull_resistor_2 (.node(pull_resistor_2_node));
  assign controlled_buffer_2_out = SetA ? ual_1_p5 : 16'bz;  // Controlled_Buffer controlled_buffer_2
  Register #(.width(16)) A (.D(controlled_buffer_2_out), .en(SetA), .clk(clk), .Q(A_q));  // open: clr
  assign pull_resistor_2_node = ReadA ? A_q : 16'bz;  // Controlled_Buffer controlled_buffer_3
  assign controlled_buffer_4_out = SetB ? ual_1_p5 : 16'bz;  // Controlled_Buffer controlled_buffer_4
  Register #(.width(16)) B (.D(controlled_buffer_4_out), .en(SetB), .clk(clk), .Q(B_q));  // open: clr
  assign pull_resistor_1_node = ReadB ? B_q : 16'bz;  // Controlled_Buffer controlled_buffer_5
  Button u_Clear (.out(Clear));
  Clock u_clk (.out(clk));
  // Probe on nothing
  // Probe on pull_resistor_1_node
  // Probe on pull_resistor_2_node
  // UAL ual_1: pin names not known; wires that end beside it: in_1, pull_resistor_1_node, pull_resistor_2_node, ual_1_p4, ual_1_p5
  // Probe on ual_1_p5

  // Other names for the same wires on the sheet: Code[3:0] = in_1

  // Notes on the sheet:
  //   S = 0 ?
endmodule
