// Logisim project archi_irq_sol.circ as structural Verilog: 2 circuits, main circuit main
module main (
);

  wire and_1_out, and_2_out, and_3_out, and_4_out, and_5_out, Bouton_out, Clear, ClearIF, Clk,
       comparator_1_eq, comparator_2_gt, comparator_3_eq, comparator_4_eq, comparator_4_gt, comparator_4_lt,
       IF, INTA, INTR, or_1_out, or_2_out, ReadA, ReadB, ReadINTAdr, ReadMem, ReadPC, ReadSP, SetA, SetB,
       SetIF, SetMem, SetPC, SetRADM, SetSP, ual_1_p10;
  wire [1:0] mcounttomux_1_mux;
  wire [2:0] CodeMCount;
  wire [3:0] binarytobcd_1_p2, binarytobcd_1_p3, binarytobcd_1_p4, binarytobcd_1_p5, binarytobcd_1_p6,
       binarytobcd_2_p2, binarytobcd_2_p3, binarytobcd_2_p4, binarytobcd_2_p5, binarytobcd_2_p6,
       binarytobcd_3_p4, binarytobcd_3_p5, binarytobcd_3_p6, binarytobcd_3_p7, binarytobcd_3_p8, UAL;
  wire [7:0] adder_1_out, Adr, MicroPC_q, multiplexer_1_out;
  wire [15:0] A_q, AdrBus, B_q, controlled_buffer_1_out, controlled_buffer_2_out, controlled_buffer_4_out,
       controlled_buffer_5_out, controlled_buffer_8_out, controlled_buffer_10_out, controlled_buffer_12_out,
       controlled_buffer_13_out, controlled_buffer_15_out, controlled_buffer_17_out, DBus, Program_counter_q,
       pull_resistor_1_node, ram_1_data, RO0_q, RO1_q, RO2_q, Stack_Pointer_q, ual_1_p8;
  wire [31:30] rom_1_data;

  assign controlled_buffer_1_out = ReadMem ? DBus : 16'bz;  // Controlled_Buffer controlled_buffer_1
  assign controlled_buffer_2_out = SetRADM ? ual_1_p8 : 16'bz;  // Controlled_Buffer controlled_buffer_2
  assign DBus = SetMem ? ual_1_p8 : 16'bz;  // Controlled_Buffer controlled_buffer_3
  and and_1 (and_1_out, SetMem, comparator_1_eq);
  Comparator #(.width(16), .mode("unsigned")) comparator_1 (
    .a(16'h1000), .b(AdrBus), .eq(comparator_1_eq));  // open: gt, lt
  Pull_Resistor pull_resistor_1 (.node(pull_resistor_1_node));
  Register #(.width(16)) Radm (.D(controlled_buffer_2_out), .en(SetRADM), .Q(AdrBus), .clk(Clk), .clr(Clear));
  Register #(.width(16)) RO0 (.D(controlled_buffer_4_out), .en(and_1_out), .Q(RO0_q), .clk(Clk), .clr(Clear));
  assign controlled_buffer_4_out = and_1_out ? DBus : 16'bz;  // Controlled_Buffer controlled_buffer_4
  assign controlled_buffer_5_out = SetMem ? DBus : 16'bz;  // Controlled_Buffer controlled_buffer_5
  Pull_Resistor pull_resistor_2 (.node(controlled_buffer_1_out));
  assign pull_resistor_1_node = ReadINTAdr ? 16'h2 : 16'bz;  // Controlled_Buffer controlled_buffer_6
  Hex_Digit_Display hex_digit_display_1 (.value(binarytobcd_1_p2));  // open: dp
  Hex_Digit_Display hex_digit_display_2 (.value(binarytobcd_1_p3));  // open: dp
  // BinaryToBCD binarytobcd_1: pin names not known; wires that end beside it: RO0_q, binarytobcd_1_p2, binarytobcd_1_p3, binarytobcd_1_p4, binarytobcd_1_p5, binarytobcd_1_p6
  Comparator #(.width(16), .mode("unsigned")) comparator_2 (
    .a(16'h1000), .b(AdrBus), .gt(comparator_2_gt));  // open: eq, lt
  Hex_Digit_Display hex_digit_display_3 (.value(binarytobcd_1_p4));  // open: dp
  Hex_Digit_Display hex_digit_display_4 (.value(binarytobcd_1_p5));  // open: dp
  RAM #(.addrWidth(16), .dataWidth(16), .bus("separate")) ram_1 (
    .addr(AdrBus), .din(controlled_buffer_5_out), .data(ram_1_data), .str(SetMem), .sel(comparator_2_gt),
    .clk(Clk), .ld(ReadMem));  // open: clr
  assign DBus = ReadMem ? ram_1_data : 16'bz;  // Controlled_Buffer controlled_buffer_7
  assign controlled_buffer_8_out = SetA ? ual_1_p8 : 16'bz;  // Controlled_Buffer controlled_buffer_8
  Hex_Digit_Display hex_digit_display_5 (.value(binarytobcd_1_p6));  // open: dp
  Button Bouton (.out(Bouton_out));
  assign pull_resistor_1_node = ReadA ? A_q : 16'bz;  // Controlled_Buffer controlled_buffer_9
  Register #(.width(16)) A (.D(controlled_buffer_8_out), .en(SetA), .Q(A_q), .clk(Clk), .clr(Clear));
  assign controlled_buffer_10_out = SetB ? ual_1_p8 : 16'bz;  // Controlled_Buffer controlled_buffer_10
  and and_2 (and_2_out, SetMem, comparator_3_eq, comparator_3_eq);
  Comparator #(.width(16), .mode("unsigned")) comparator_3 (
    .a(16'h1001), .b(AdrBus), .eq(comparator_3_eq));  // open: gt, lt
  or or_1 (or_1_out, Clear, and_3_out);
  and and_3 (and_3_out, Clk, INTA);
  assign controlled_buffer_1_out = ReadB ? B_q : 16'bz;  // Controlled_Buffer controlled_buffer_11
  Register #(.width(16)) B (.D(controlled_buffer_10_out), .en(SetB), .Q(B_q), .clk(Clk), .clr(Clear));
  Register #(.width(16)) RO1 (.D(controlled_buffer_12_out), .en(and_2_out), .Q(RO1_q), .clk(Clk), .clr(Clear));
  assign controlled_buffer_12_out = and_2_out ? DBus : 16'bz;  // Controlled_Buffer controlled_buffer_12
  D_Flip_Flop d_ff_1 (.clk(Bouton_out), .D(1'b1), .Q(INTR), .en(1'b1), .reset(or_1_out));  // open: Qn, preset
  assign controlled_buffer_13_out = SetPC ? ual_1_p8 : 16'bz;  // Controlled_Buffer controlled_buffer_13
  Hex_Digit_Display hex_digit_display_6 (.value(binarytobcd_2_p2));  // open: dp
  Hex_Digit_Display hex_digit_display_7 (.value(binarytobcd_2_p3));  // open: dp
  // BinaryToBCD binarytobcd_2: pin names not known; wires that end beside it: RO1_q, binarytobcd_2_p2, binarytobcd_2_p3, binarytobcd_2_p4, binarytobcd_2_p5, binarytobcd_2_p6
  assign pull_resistor_1_node = ReadPC ? Program_counter_q : 16'bz;  // Controlled_Buffer controlled_buffer_14
  Register #(.width(16)) Program_counter (
    .D(controlled_buffer_13_out), .en(SetPC), .Q(Program_counter_q), .clk(Clk), .clr(Clear));
  Hex_Digit_Display hex_digit_display_8 (.value(binarytobcd_2_p5));  // open: dp
  Hex_Digit_Display hex_digit_display_9 (.value(binarytobcd_2_p4));  // open: dp
  Adder adder_1 (.a(MicroPC_q), .b(8'h1), .out(adder_1_out), .cin(1'b0));  // open: cout
  assign controlled_buffer_15_out = SetSP ? ual_1_p8 : 16'bz;  // Controlled_Buffer controlled_buffer_15
  Hex_Digit_Display hex_digit_display_10 (.value(binarytobcd_2_p6));  // open: dp
  assign pull_resistor_1_node = ReadSP ? Stack_Pointer_q : 16'bz;  // Controlled_Buffer controlled_buffer_16
  Register #(.width(16)) Stack_Pointer (
    .D(controlled_buffer_15_out), .en(SetSP), .Q(Stack_Pointer_q), .clk(Clk), .clr(Clear));
  Comparator #(.width(16), .mode("unsigned")) comparator_4 (
    .a(16'h1002), .b(AdrBus), .gt(comparator_4_gt), .eq(comparator_4_eq), .lt(comparator_4_lt));
  Multiplexer #(.select(2), .width(8)) multiplexer_1 (
    .in0(adder_1_out), .in1(Adr), .in2(controlled_buffer_1_out[15:8]), .out(multiplexer_1_out),
    .sel(mcounttomux_1_mux), .en(1'b1));  // open: in3
  MCountToMux mcounttomux_1 (.INT(and_5_out), .MCount(CodeMCount), .Z(ual_1_p10), .Mux(mcounttomux_1_mux));
  or or_2 (or_2_out, ClearIF, ClearIF, SetIF, SetIF);
  and and_4 (and_4_out, SetMem, comparator_4_gt, comparator_4_eq, comparator_4_lt);
  assign controlled_buffer_17_out = and_4_out ? DBus : 16'bz;  // Controlled_Buffer controlled_buffer_17
  and and_5 (and_5_out, IF, INTR);
  D_Flip_Flop Interrupt_Flag (.clk(Clk), .D(SetIF), .Q(IF), .en(or_2_out), .reset(Clear));  // open: Qn, preset
  Hex_Digit_Display hex_digit_display_11 (.value(binarytobcd_3_p4));  // open: dp
  Register #(.width(16)) RO2 (.D(controlled_buffer_17_out), .en(and_4_out), .Q(RO2_q), .clk(Clk), .clr(Clear));
  Button button_1 (.out(Clear));
  Clock clock_1 (.out(Clk));
  Register MicroPC (.D(multiplexer_1_out), .en(1'b1), .Q(MicroPC_q), .clk(Clk), .clr(Clear));
  Hex_Digit_Display hex_digit_display_12 (.value(binarytobcd_3_p6));  // open: dp
  Hex_Digit_Display hex_digit_display_13 (.value(binarytobcd_3_p5));  // open: dp
  // BinaryToBCD binarytobcd_3: pin names not known; wires that end beside it: SetMem, comparator_4_eq, RO2_q, binarytobcd_3_p4, binarytobcd_3_p5, binarytobcd_3_p6, binarytobcd_3_p7, binarytobcd_3_p8
  // UAL ual_1: pin names not known; wires that end beside it: SetIF, IF, INTR, UAL[1], pull_resistor_1_node, UAL[2], UAL[3], ual_1_p8, controlled_buffer_1_out, ual_1_p10, ual_1_p10
  Hex_Digit_Display hex_digit_display_14 (.value(binarytobcd_3_p8));  // open: dp
  Hex_Digit_Display hex_digit_display_15 (.value(binarytobcd_3_p7));  // open: dp
  ROM #(.dataWidth(32)) rom_1 (
    .addr(MicroPC_q),
    .data({rom_1_data, ReadINTAdr, ClearIF, SetIF, INTA, CodeMCount, UAL, SetSP, ReadSP, SetB, ReadB, SetA, ReadA, SetPC, ReadPC, SetRADM, SetMem, ReadMem, Adr}),
    .sel(1'b1));
  Pull_Resistor pull_resistor_3 (.node(DBus));
  Pull_Resistor pull_resistor_4 (.node(AdrBus));

  // Notes on the sheet:
  //   Bus Adresse
  //   Bus Données
  //   Bus B
  //   Bus A
  //   Bus Données
  //   Bus Adresse
  //   InstCode
  //   Bus S
  //   S = 0 ?
  //   contents of rom_1 (hex, n*v repeats v):
  //   2000008 8000e0 6*0 c00 1401900 0 0 80000c 0 0 0 c00 84100 c01800 0 c00 80500 84100 c01800 4*0 c00
  //   80500 2200 c01800 c00 90100 c01800 0 c00 80500 90100 c01800 4*0 c00 80500 8a200 c01800 b0e000 0 0 0
  //   b1a000 0 0 0 b8e000 0 0 0 b9a000 0 0 0 d0e000 0 0 0 d1a000 0 0 0 d86000 7*0 90e000 0 0 0 91a000 0 0
  //   0 98e000 0 0 0 99a000 0 0 0 a06000 0 0 0 a98000 11*0 c00 881100 0 0 1802076 c01800 c00 881100
  //   188807a c01800 c00 881100 4*0 c00 c0100 c01800 0 c00 80500 c0100 c01800 4*0 c00 80500 20200 c01800
  //   c60000 0 0 0 ce0000 11*0 20400 400a00 4e0000 c00 881100 0 0 0 460400 881100 6*0 20400 2200 ce0000 0
  //   460400 884100 0 0 c00 320500 2200 c01800 c00 320500 84100 c01800 20400 88200 ce0000 0 460400 890100
  //   0 0 c00 320500 88200 c01800 c00 320500 90100 c01800 10800000 0 0 0 8800000 11*0 14020400 2200 4e0400
  //   88200 4e0400 a00 4e0000 20801008 460400 81100 460400 90100 460400 8884100
endmodule

module MCountToMux (
  input  INT,
  input  [2:0] MCount,
  input  Z,
  output [1:0] Mux
);

  wire and_2_out, and_3_out, and_4_out, not_1_out, not_2_out, not_3_out, not_4_out;

  not not_1 (not_1_out, INT);
  not not_2 (not_2_out, MCount[1]);
  not not_3 (not_3_out, MCount[0]);
  not not_4 (not_4_out, Z);
  and and_1 (Mux[1], MCount[1], not_3_out);
  and and_2 (and_2_out, not_2_out, MCount[0]);
  and and_3 (and_3_out, MCount[1], MCount[0], Z);
  and and_4 (and_4_out, not_1_out, MCount[2]);
  or or_1 (Mux[0], and_2_out, and_3_out, and_4_out);
endmodule
