// Logisim project timer.circ as structural Verilog: 1 circuit, main circuit main
module main (
  input  in_1,
  output out_2
);

  wire and_1_out, and_2_out, Clear, Clk, comparator_1_lt, or_1_out, or_2_out;
  wire [15:0] counter_1_q;

  Button button_1 (.out(Clear));
  Clock clock_1 (.out(Clk));
  Counter #(.width(16), .max('hffff)) counter_1 (
    .count(1'b1), .Q(counter_1_q), .clk(Clk), .clr(or_1_out));  // open: load, D, carry
  and and_1 (and_1_out, Clk, comparator_1_lt);
  Comparator #(.width(16), .mode("unsigned")) comparator_1 (
    .a(16'hfff), .b(counter_1_q), .lt(comparator_1_lt));  // open: gt, eq
  or or_1 (or_1_out, and_1_out, Clear);
  D_Flip_Flop d_ff_1 (.clk(comparator_1_lt), .D(1'b1), .Q(out_2), .en(1'b1), .reset(or_2_out));  // open: Qn, preset
  or or_2 (or_2_out, and_2_out, Clear);
  and and_2 (and_2_out, Clk, in_1);

  // Other names for the same wires on the sheet: INTA = in_1; INTR = out_2
endmodule
