// Logisim project archi_irq_clavier.circ as structural Verilog: 2 circuits, main circuit main
module main (
);

  wire and_1_out, and_2_out, and_3_out, and_4_out, and_5_out, and_6_out, Clear, ClearIF, Clk,
       comparator_1_eq, comparator_1_gt, comparator_1_lt, comparator_2_eq, comparator_3_gt, comparator_4_eq,
       comparator_5_eq, comparator_6_eq, comparator_6_gt, comparator_6_lt, IF, INTA, INTR, or_1_out, ReadA,
       ReadB, ReadINTAdr, ReadMem, ReadPC, ReadSP, SetA, SetB, SetIF, SetMem, SetPC, SetRADM, SetSP,
       ual_1_p10;
  wire [1:0] mcounttomux_1_mux;
  wire [2:0] CodeMCount;
  wire [3:0] binarytobcd_1_p2, binarytobcd_1_p3, binarytobcd_1_p4, binarytobcd_1_p5, binarytobcd_1_p6,
       binarytobcd_2_p2, binarytobcd_2_p3, binarytobcd_2_p4, binarytobcd_2_p5, binarytobcd_2_p6,
       binarytobcd_3_p4, binarytobcd_3_p5, binarytobcd_3_p6, binarytobcd_3_p7, binarytobcd_3_p8, UAL;
  wire [6:0] keyboard_1_data, register_1_q;
  wire [7:0] adder_1_out, Adr, controlled_buffer_2_out, controlled_buffer_2_out_2, MicroPC_q,
       multiplexer_1_out;
  wire [15:0] A_q, AdrBus, B_q, controlled_buffer_1_out, controlled_buffer_3_out, controlled_buffer_5_out,
       controlled_buffer_6_out, controlled_buffer_9_out, controlled_buffer_11_out, controlled_buffer_13_out,
       controlled_buffer_14_out, controlled_buffer_16_out, controlled_buffer_19_out, DBus, Program_counter_q,
       pull_resistor_1_node, ram_1_data, RO0_q, RO1_q, RO2_q, Stack_Pointer_q, ual_1_p8;
  wire [31:30] rom_1_data;

  Comparator #(.width(16), .mode("unsigned")) comparator_1 (
    .a(16'h1004), .b(AdrBus), .gt(comparator_1_gt), .eq(comparator_1_eq), .lt(comparator_1_lt));
  assign controlled_buffer_1_out = and_1_out ? DBus : 16'bz;  // Controlled_Buffer controlled_buffer_1
  and and_1 (and_1_out, SetMem, comparator_1_gt, comparator_1_eq, comparator_1_lt);
  assign {controlled_buffer_2_out_2, controlled_buffer_2_out} = ReadMem ? DBus : 16'bz;  // Controlled_Buffer controlled_buffer_2
  assign controlled_buffer_3_out = SetRADM ? ual_1_p8 : 16'bz;  // Controlled_Buffer controlled_buffer_3
  assign DBus = SetMem ? ual_1_p8 : 16'bz;  // Controlled_Buffer controlled_buffer_4
  and and_2 (and_2_out, SetMem, comparator_2_eq);
  Comparator #(.width(16), .mode("unsigned")) comparator_2 (
    .a(16'h1000), .b(AdrBus), .eq(comparator_2_eq));  // open: gt, lt
  TTY tty_1 (.data(controlled_buffer_1_out[6:0]), .clk(Clk), .we(and_1_out), .clr(Clear));
  Pull_Resistor pull_resistor_1 (.node(pull_resistor_1_node));
  Register #(.width(16)) Radm (.D(controlled_buffer_3_out), .en(SetRADM), .Q(AdrBus), .clk(Clk), .clr(Clear));
  Register #(.width(16)) RO0 (.D(controlled_buffer_5_out), .en(and_2_out), .Q(RO0_q), .clk(Clk), .clr(Clear));
  assign controlled_buffer_5_out = and_2_out ? DBus : 16'bz;  // Controlled_Buffer controlled_buffer_5
  assign controlled_buffer_6_out = SetMem ? DBus : 16'bz;  // Controlled_Buffer controlled_buffer_6
  Pull_Resistor pull_resistor_2 (.node({controlled_buffer_2_out_2, controlled_buffer_2_out}));
  assign pull_resistor_1_node = ReadINTAdr ? 16'h2 : 16'bz;  // Controlled_Buffer controlled_buffer_7
  Hex_Digit_Display hex_digit_display_1 (.value(binarytobcd_1_p3));  // open: dp
  Hex_Digit_Display hex_digit_display_2 (.value(binarytobcd_1_p2));  // open: dp
  // BinaryToBCD binarytobcd_1: pin names not known; wires that end beside it: RO0_q, binarytobcd_1_p2, binarytobcd_1_p3, binarytobcd_1_p4, binarytobcd_1_p5, binarytobcd_1_p6
  Comparator #(.width(16), .mode("unsigned")) comparator_3 (
    .a(16'h1000), .b(AdrBus), .gt(comparator_3_gt));  // open: eq, lt
  Hex_Digit_Display hex_digit_display_3 (.value(binarytobcd_1_p5));  // open: dp
  Hex_Digit_Display hex_digit_display_4 (.value(binarytobcd_1_p4));  // open: dp
  RAM #(.addrWidth(16), .dataWidth(16), .bus("separate")) ram_1 (
    .addr(AdrBus), .din(controlled_buffer_6_out), .data(ram_1_data), .str(SetMem), .sel(comparator_3_gt),
    .clk(Clk), .ld(ReadMem));  // open: clr
  assign DBus = ReadMem ? ram_1_data : 16'bz;  // Controlled_Buffer controlled_buffer_8
  assign controlled_buffer_9_out = SetA ? ual_1_p8 : 16'bz;  // Controlled_Buffer controlled_buffer_9
  Hex_Digit_Display hex_digit_display_5 (.value(binarytobcd_1_p6));  // open: dp
  assign pull_resistor_1_node = ReadA ? A_q : 16'bz;  // Controlled_Buffer controlled_buffer_10
  Register #(.width(16)) A (.D(controlled_buffer_9_out), .en(SetA), .Q(A_q), .clk(Clk), .clr(Clear));
  assign controlled_buffer_11_out = SetB ? ual_1_p8 : 16'bz;  // Controlled_Buffer controlled_buffer_11
  and and_3 (and_3_out, SetMem, comparator_4_eq, comparator_4_eq);
  Comparator #(.width(16), .mode("unsigned")) comparator_4 (
    .a(16'h1001), .b(AdrBus), .eq(comparator_4_eq));  // open: gt, lt
  assign {controlled_buffer_2_out_2, controlled_buffer_2_out} = ReadB ? B_q : 16'bz;  // Controlled_Buffer controlled_buffer_12
  Register #(.width(16)) B (.D(controlled_buffer_11_out), .en(SetB), .Q(B_q), .clk(Clk), .clr(Clear));
  Register #(.width(16)) RO1 (.D(controlled_buffer_13_out), .en(and_3_out), .Q(RO1_q), .clk(Clk), .clr(Clear));
  assign controlled_buffer_13_out = and_3_out ? DBus : 16'bz;  // Controlled_Buffer controlled_buffer_13
  Keyboard #(.buflen(1)) keyboard_1 (.clk(Clk), .re(INTA), .clr(Clear), .avail(INTR), .data(keyboard_1_data));
  assign controlled_buffer_14_out = SetPC ? ual_1_p8 : 16'bz;  // Controlled_Buffer controlled_buffer_14
  Hex_Digit_Display hex_digit_display_6 (.value(binarytobcd_2_p2));  // open: dp
  Hex_Digit_Display hex_digit_display_7 (.value(binarytobcd_2_p3));  // open: dp
  // BinaryToBCD binarytobcd_2: pin names not known; wires that end beside it: RO1_q, binarytobcd_2_p2, binarytobcd_2_p3, binarytobcd_2_p4, binarytobcd_2_p5, binarytobcd_2_p6
  assign pull_resistor_1_node = ReadPC ? Program_counter_q : 16'bz;  // Controlled_Buffer controlled_buffer_15
  Register #(.width(16)) Program_counter (
    .D(controlled_buffer_14_out), .en(SetPC), .Q(Program_counter_q), .clk(Clk), .clr(Clear));
  Hex_Digit_Display hex_digit_display_8 (.value(binarytobcd_2_p5));  // open: dp
  Hex_Digit_Display hex_digit_display_9 (.value(binarytobcd_2_p4));  // open: dp
  Comparator #(.width(16), .mode("unsigned")) comparator_5 (
    .a(16'h1003), .b(AdrBus), .eq(comparator_5_eq));  // open: gt, lt
  Adder adder_1 (.a(MicroPC_q), .b(8'h1), .out(adder_1_out), .cin(1'b0));  // open: cout
  assign controlled_buffer_16_out = SetSP ? ual_1_p8 : 16'bz;  // Controlled_Buffer controlled_buffer_16
  Hex_Digit_Display hex_digit_display_10 (.value(binarytobcd_2_p6));  // open: dp
  Register #(.width(7)) register_1 (.D(keyboard_1_data), .en(INTA), .Q(register_1_q), .clk(Clk), .clr(Clear));
  and and_4 (and_4_out, ReadMem, comparator_5_eq);
  assign pull_resistor_1_node = ReadSP ? Stack_Pointer_q : 16'bz;  // Controlled_Buffer controlled_buffer_17
  Register #(.width(16)) Stack_Pointer (
    .D(controlled_buffer_16_out), .en(SetSP), .Q(Stack_Pointer_q), .clk(Clk), .clr(Clear));
  Comparator #(.width(16), .mode("unsigned")) comparator_6 (
    .a(16'h1002), .b(AdrBus), .gt(comparator_6_gt), .eq(comparator_6_eq), .lt(comparator_6_lt));
  assign DBus = and_4_out ? {{9{1'b0}}, register_1_q} : 16'bz;  // Controlled_Buffer controlled_buffer_18
  Multiplexer #(.select(2), .width(8)) multiplexer_1 (
    .in0(adder_1_out), .in1(Adr), .in2(controlled_buffer_2_out_2), .out(multiplexer_1_out),
    .sel(mcounttomux_1_mux), .en(1'b1));  // open: in3
  MCountToMux mcounttomux_1 (.INT(and_6_out), .MCount(CodeMCount), .Z(ual_1_p10), .Mux(mcounttomux_1_mux));
  or or_1 (or_1_out, ClearIF, ClearIF, SetIF, SetIF);
  and and_5 (and_5_out, SetMem, comparator_6_gt, comparator_6_eq, comparator_6_lt);
  assign controlled_buffer_19_out = and_5_out ? DBus : 16'bz;  // Controlled_Buffer controlled_buffer_19
  and and_6 (and_6_out, IF, INTR);
  D_Flip_Flop Interrupt_Flag (.clk(Clk), .D(SetIF), .Q(IF), .en(or_1_out), .reset(Clear));  // open: Qn, preset
  Hex_Digit_Display hex_digit_display_11 (.value(binarytobcd_3_p4));  // open: dp
  Register #(.width(16)) RO2 (.D(controlled_buffer_19_out), .en(and_5_out), .Q(RO2_q), .clk(Clk), .clr(Clear));
  Button button_1 (.out(Clear));
  Clock clock_1 (.out(Clk));
  Register MicroPC (.D(multiplexer_1_out), .en(1'b1), .Q(MicroPC_q), .clk(Clk), .clr(Clear));
  Hex_Digit_Display hex_digit_display_12 (.value(binarytobcd_3_p6));  // open: dp
  Hex_Digit_Display hex_digit_display_13 (.value(binarytobcd_3_p5));  // open: dp
  // BinaryToBCD binarytobcd_3: pin names not known; wires that end beside it: SetMem, comparator_6_eq, RO2_q, binarytobcd_3_p4, binarytobcd_3_p5, binarytobcd_3_p6, binarytobcd_3_p7, binarytobcd_3_p8
  // UAL ual_1: pin names not known; wires that end beside it: SetIF, IF, INTR, UAL[1], pull_resistor_1_node, UAL[2], UAL[3], ual_1_p8, {controlled_buffer_2_out_2, controlled_buffer_2_out}, ual_1_p10, ual_1_p10
  Hex_Digit_Display hex_digit_display_14 (.value(binarytobcd_3_p7));  // open: dp
  Hex_Digit_Display hex_digit_display_15 (.value(binarytobcd_3_p8));  // open: dp
  ROM #(.dataWidth(32)) rom_1 (
    .addr(MicroPC_q),
    .data({rom_1_data, ReadINTAdr, ClearIF, SetIF, INTA, CodeMCount, UAL, SetSP, ReadSP, SetB, ReadB, SetA, ReadA, SetPC, ReadPC, SetRADM, SetMem, ReadMem, Adr}),
    .sel(1'b1));
  Pull_Resistor pull_resistor_3 (.node(DBus));
  Pull_Resistor pull_resistor_4 (.node(AdrBus));

  // Notes on the sheet:
  //   Bus Adresse
  //   Bus Données
  //   Bus B
  //   Bus A
  //   Bus Données
  //   Bus Adresse
  //   InstCode
  //   Bus S
  //   S = 0 ?
endmodule

module MCountToMux (
  input  INT,
  input  [2:0] MCount,
  input  Z,
  output [1:0] Mux
);

  wire and_2_out, and_3_out, and_4_out, not_1_out, not_2_out, not_3_out, not_4_out;

  not not_1 (not_1_out, INT);
  not not_2 (not_2_out, MCount[1]);
  not not_3 (not_3_out, MCount[0]);
  not not_4 (not_4_out, Z);
  and and_1 (Mux[1], MCount[1], not_3_out);
  and and_2 (and_2_out, not_2_out, MCount[0]);
  and and_3 (and_3_out, MCount[1], MCount[0], Z);
  and and_4 (and_4_out, not_1_out, MCount[2]);
  or or_1 (Mux[0], and_2_out, and_3_out, and_4_out);
endmodule
