// Logisim project archi_seq_man.circ as structural Verilog: 1 circuit, main circuit main
module main (
  input  [3:0] UAL,
  input  SetB,
  input  ReadB,
  input  SetA,
  input  ReadA,
  input  SetPC,
  input  ReadPC,
  input  SetRADM,
  input  SetMem,
  input  ReadMem,
  output S___0
);

  wire and_1_out, and_2_out, and_3_out, Clear, Clk, comparator_1_eq, comparator_2_gt, comparator_3_eq,
       comparator_4_eq, comparator_4_gt, comparator_4_lt;
  wire [3:0] binarytobcd_1_p2, binarytobcd_1_p3, binarytobcd_1_p4, binarytobcd_1_p5, binarytobcd_1_p6,
       binarytobcd_2_p2, binarytobcd_2_p3, binarytobcd_2_p4, binarytobcd_2_p5, binarytobcd_2_p6,
       binarytobcd_3_p4, binarytobcd_3_p5, binarytobcd_3_p6, binarytobcd_3_p7, binarytobcd_3_p8;
  wire [15:0] A_q, AdrBus, B_q, controlled_buffer_1_out, controlled_buffer_3_out, controlled_buffer_4_out,
       controlled_buffer_5_out, controlled_buffer_6_out, controlled_buffer_9_out, controlled_buffer_11_out,
       controlled_buffer_12_out, controlled_buffer_14_out, DBus, PC_q, pull_resistor_1_node, ram_1_data,
       RO0_q, RO1_q, RO2_q, ual_1_p5;

  and and_1 (and_1_out, SetMem, comparator_1_eq);
  Comparator #(.width(16), .mode("unsigned")) comparator_1 (
    .a(16'h1000), .b(AdrBus), .eq(comparator_1_eq));  // open: gt, lt
  Pull_Resistor pull_resistor_1 (.node(pull_resistor_1_node));
  assign controlled_buffer_1_out = ReadMem ? DBus : 16'bz;  // Controlled_Buffer controlled_buffer_1
  assign DBus = SetMem ? ual_1_p5 : 16'bz;  // Controlled_Buffer controlled_buffer_2
  Register #(.width(16)) RO0 (.D(controlled_buffer_3_out), .en(and_1_out), .Q(RO0_q), .clk(Clk), .clr(Clear));
  assign controlled_buffer_3_out = and_1_out ? DBus : 16'bz;  // Controlled_Buffer controlled_buffer_3
  assign controlled_buffer_4_out = SetMem ? DBus : 16'bz;  // Controlled_Buffer controlled_buffer_4
  Pull_Resistor pull_resistor_2 (.node(controlled_buffer_1_out));
  assign controlled_buffer_5_out = SetRADM ? ual_1_p5 : 16'bz;  // Controlled_Buffer controlled_buffer_5
  Hex_Digit_Display hex_digit_display_1 (.value(binarytobcd_1_p3));  // open: dp
  Hex_Digit_Display hex_digit_display_2 (.value(binarytobcd_1_p2));  // open: dp
  // BinaryToBCD binarytobcd_1: pin names not known; wires that end beside it: RO0_q, binarytobcd_1_p2, binarytobcd_1_p3, binarytobcd_1_p4, binarytobcd_1_p5, binarytobcd_1_p6
  Comparator #(.width(16), .mode("unsigned")) comparator_2 (
    .a(16'h1000), .b(AdrBus), .gt(comparator_2_gt));  // open: eq, lt
  Register #(.width(16)) Radm (.D(controlled_buffer_5_out), .en(SetRADM), .Q(AdrBus), .clk(Clk), .clr(Clear));
  assign controlled_buffer_6_out = SetA ? ual_1_p5 : 16'bz;  // Controlled_Buffer controlled_buffer_6
  Hex_Digit_Display hex_digit_display_3 (.value(binarytobcd_1_p4));  // open: dp
  Hex_Digit_Display hex_digit_display_4 (.value(binarytobcd_1_p5));  // open: dp
  RAM #(.addrWidth(16), .dataWidth(16), .bus("separate")) ram_1 (
    .addr(AdrBus), .din(controlled_buffer_4_out), .data(ram_1_data), .str(SetMem), .sel(comparator_2_gt),
    .clk(Clk), .ld(ReadMem));  // open: clr
  assign DBus = ReadMem ? ram_1_data : 16'bz;  // Controlled_Buffer controlled_buffer_7
  Hex_Digit_Display hex_digit_display_5 (.value(binarytobcd_1_p6));  // open: dp
  assign pull_resistor_1_node = ReadA ? A_q : 16'bz;  // Controlled_Buffer controlled_buffer_8
  Register #(.width(16)) A (.D(controlled_buffer_6_out), .en(SetA), .Q(A_q), .clk(Clk), .clr(Clear));
  assign controlled_buffer_9_out = SetB ? ual_1_p5 : 16'bz;  // Controlled_Buffer controlled_buffer_9
  and and_2 (and_2_out, SetMem, comparator_3_eq, comparator_3_eq);
  Comparator #(.width(16), .mode("unsigned")) comparator_3 (
    .a(16'h1001), .b(AdrBus), .eq(comparator_3_eq));  // open: gt, lt
  assign controlled_buffer_1_out = ReadB ? B_q : 16'bz;  // Controlled_Buffer controlled_buffer_10
  Register #(.width(16)) B (.D(controlled_buffer_9_out), .en(SetB), .Q(B_q), .clk(Clk), .clr(Clear));
  Register #(.width(16)) RO1 (.D(controlled_buffer_11_out), .en(and_2_out), .Q(RO1_q), .clk(Clk), .clr(Clear));
  assign controlled_buffer_11_out = and_2_out ? DBus : 16'bz;  // Controlled_Buffer controlled_buffer_11
  assign controlled_buffer_12_out = SetPC ? ual_1_p5 : 16'bz;  // Controlled_Buffer controlled_buffer_12
  Hex_Digit_Display hex_digit_display_6 (.value(binarytobcd_2_p2));  // open: dp
  Hex_Digit_Display hex_digit_display_7 (.value(binarytobcd_2_p3));  // open: dp
  // BinaryToBCD binarytobcd_2: pin names not known; wires that end beside it: RO1_q, binarytobcd_2_p2, binarytobcd_2_p3, binarytobcd_2_p4, binarytobcd_2_p5, binarytobcd_2_p6
  assign pull_resistor_1_node = ReadPC ? PC_q : 16'bz;  // Controlled_Buffer controlled_buffer_13
  Register #(.width(16)) PC (.D(controlled_buffer_12_out), .en(SetPC), .Q(PC_q), .clk(Clk), .clr(Clear));
  Hex_Digit_Display hex_digit_display_8 (.value(binarytobcd_2_p4));  // open: dp
  Hex_Digit_Display hex_digit_display_9 (.value(binarytobcd_2_p5));  // open: dp
  Hex_Digit_Display hex_digit_display_10 (.value(binarytobcd_2_p6));  // open: dp
  Comparator #(.width(16), .mode("unsigned")) comparator_4 (
    .a(16'h1002), .b(AdrBus), .gt(comparator_4_gt), .eq(comparator_4_eq), .lt(comparator_4_lt));
  and and_3 (and_3_out, SetMem, comparator_4_gt, comparator_4_eq, comparator_4_lt);
  assign controlled_buffer_14_out = and_3_out ? DBus : 16'bz;  // Controlled_Buffer controlled_buffer_14
  Button button_1 (.out(Clear));
  Clock clock_1 (.out(Clk));
  Hex_Digit_Display hex_digit_display_11 (.value(binarytobcd_3_p4));  // open: dp
  Register #(.width(16)) RO2 (.D(controlled_buffer_14_out), .en(and_3_out), .Q(RO2_q), .clk(Clk), .clr(Clear));
  Hex_Digit_Display hex_digit_display_12 (.value(binarytobcd_3_p6));  // open: dp
  Hex_Digit_Display hex_digit_display_13 (.value(binarytobcd_3_p5));  // open: dp
  // BinaryToBCD binarytobcd_3: pin names not known; wires that end beside it: SetMem, comparator_4_eq, RO2_q, binarytobcd_3_p4, binarytobcd_3_p5, binarytobcd_3_p6, binarytobcd_3_p7, binarytobcd_3_p8
  // UAL ual_1: pin names not known; wires that end beside it: UAL[1], pull_resistor_1_node, UAL[2], UAL[3], ual_1_p5, controlled_buffer_1_out, S___0
  Hex_Digit_Display hex_digit_display_14 (.value(binarytobcd_3_p7));  // open: dp
  Hex_Digit_Display hex_digit_display_15 (.value(binarytobcd_3_p8));  // open: dp
  Pull_Resistor pull_resistor_3 (.node(DBus));
  Pull_Resistor pull_resistor_4 (.node(AdrBus));

  // Notes on the sheet:
  //   Bus Adresse
  //   Bus Données
  //   Bus B
  //   Bus A
  //   Bus Données
  //   Bus Adresse
  //   Bus S
endmodule
